// Logisim project Travel_Clock.circ as structural Verilog: 36 circuits, main circuit main
module main (
  input  MODE_BTN,
  input  Start_stop_set_BTN,
  input  BTN_SP,
  input  CHA,
  input  CHB,
  output Buzzer,
  output VDD,
  output GND
);

  wire affich_1_a, affich_1_b, affich_1_c, affich_1_d, affich_1_e, affich_1_f, affich_1_g, affich_2_a,
       affich_2_b, affich_2_c, affich_2_d, affich_2_e, affich_2_f, affich_2_g, affich_3_a, affich_3_b,
       affich_3_c, affich_3_d, affich_3_e, affich_3_f, affich_3_g, affich_4_a, affich_4_b, affich_4_c,
       affich_4_d, affich_4_e, affich_4_f, affich_4_g, affich_5_a, affich_5_b, affich_5_c, affich_5_d,
       affich_5_e, affich_5_f, affich_5_g, affich_6_a, affich_6_b, affich_6_c, affich_6_d, affich_6_e,
       affich_6_f, affich_6_g, ALARME_1_buzz, ALARME_1_set_ok, and_1_out, and_2_out, Anim_LED_1_ledr1,
       Anim_LED_1_ledr2, Anim_LED_1_ledr3, Anim_LED_1_ledr4, Anim_LED_1_ledr5, Anim_LED_1_ledr6,
       Anim_LED_1_ledr7, Anim_LED_1_ledr8, Anim_LED_1_ledr9, ButtonDeb_1_s, ButtonDeb_2_s, ButtonspeDeb_s,
       clock_1_out, comparator_1_eq, comparator_2_eq, counter_1_carry, counter_2_carry, counter_3_carry,
       demultiplexer_1_out0, demultiplexer_1_out1, demultiplexer_1_out2, demultiplexer_1_out3,
       DipSwitch_1_sw1, DipSwitch_1_sw10, HEURE_1_set_ok, JEUMEMORY_1_led1, JEUMEMORY_1_led2,
       JEUMEMORY_1_led3, JEUMEMORY_1_led4, JEUMEMORY_1_led5, JEUMEMORY_1_led6, JEUMEMORY_1_led7,
       JEUMEMORY_1_led8, JEUSWITCH_1_led1, JEUSWITCH_1_led2, JEUSWITCH_1_led3, JEUSWITCH_1_led4,
       JEUSWITCH_1_led5, JEUSWITCH_1_led6, JEUSWITCH_1_led7, JEUSWITCH_1_led8, MINUTEUR_1_buzz,
       MINUTEUR_1_set_ok, multiplexer_6_out, multiplexer_7_out, multiplexer_8_out, multiplexer_9_out,
       multiplexer_10_out, multiplexer_11_out, multiplexer_12_out, multiplexer_13_out, not_1_out, or_1_out,
       or_2_out, or_3_out, or_4_out, s_r_ff_1_q, s_r_ff_2_q;
  wire [1:0] demultiplexer_1_out4;
  wire [3:0] ALARME_1_d_h_set_alarm, ALARME_1_d_min_set_alarm, ALARME_1_u_h_set_alarm,
       ALARME_1_u_min_set_alarm, CHRONO_1_d_min_chrono, CHRONO_1_d_sec_chrono, CHRONO_1_u_h_chrono,
       CHRONO_1_u_min_chrono, CHRONO_1_u_sec_chrono, HEURE_1_d_h_now, HEURE_1_d_min_now, HEURE_1_u_h_now,
       HEURE_1_u_min_now, JEUMEMORY_1_d_point, JEUMEMORY_1_tps, JEUMEMORY_1_u_point, JEUSWITCH_1_d_point,
       JEUSWITCH_1_d_sec_jeu, JEUSWITCH_1_u_point, JEUSWITCH_1_u_sec_jeu, MINUTEUR_1_d_min_timer,
       MINUTEUR_1_d_sec_timer, MINUTEUR_1_u_h_timer, MINUTEUR_1_u_min_timer, MINUTEUR_1_u_sec_timer,
       mode_1_mode, multiplexer_1_out, multiplexer_2_out, multiplexer_3_out, multiplexer_4_out,
       multiplexer_5_out;
  wire [7:0] DipSwitch_1_sw9;
  wire [8:0] counter_3_q;
  wire [10:0] counter_2_q;

  Clock clock_1 (.out(clock_1_out));
  ButtonDeb ButtonspeDeb (.E(BTN_SP), .Clock(clock_1_out), .Reset(DipSwitch_1_sw10), .S(ButtonspeDeb_s));
  DipSwitch #(.number(10)) DipSwitch_1 (
    .sw1(DipSwitch_1_sw1), .sw2(DipSwitch_1_sw9[7]), .sw3(DipSwitch_1_sw9[6]), .sw4(DipSwitch_1_sw9[5]),
    .sw5(DipSwitch_1_sw9[4]), .sw6(DipSwitch_1_sw9[3]), .sw7(DipSwitch_1_sw9[2]), .sw8(DipSwitch_1_sw9[1]),
    .sw9(DipSwitch_1_sw9[0]), .sw10(DipSwitch_1_sw10));
  not not_1 (not_1_out, Start_stop_set_BTN);
  ButtonDeb ButtonDeb_1 (.E(MODE_BTN), .Clock(clock_1_out), .Reset(DipSwitch_1_sw10), .S(ButtonDeb_1_s));
  ButtonDeb ButtonDeb_2 (.E(not_1_out), .Clock(clock_1_out), .Reset(DipSwitch_1_sw10), .S(ButtonDeb_2_s));
  Demultiplexer #(.select(3), .enable("false")) demultiplexer_1 (
    .out0(demultiplexer_1_out0), .out1(demultiplexer_1_out1), .out2(demultiplexer_1_out2),
    .out3(demultiplexer_1_out3), .out4(demultiplexer_1_out4[0]), .out5(demultiplexer_1_out4[1]), .in(1'b1),
    .sel(mode_1_mode[2:0]));  // open: out6, out7
  affich affich_1 (
    .a0(mode_1_mode[3]), .b0(mode_1_mode[2]), .c0(mode_1_mode[1]), .d0(mode_1_mode[0]), .a(affich_1_a),
    .b(affich_1_b), .c(affich_1_c), .d(affich_1_d), .e(affich_1_e), .f(affich_1_f), .g(affich_1_g));
  mode mode_1 (.MODE_BTN(ButtonDeb_1_s), .Clock(clock_1_out), .Reset(DipSwitch_1_sw10), .Mode(mode_1_mode));
  _7_Segment_Display L_7_Segment_Display_1 (
    .g(affich_1_g), .f(affich_1_f), .a(affich_1_a), .b(affich_1_b), .e(affich_1_e), .d(affich_1_d),
    .c(affich_1_c), .dp(1'b1));
  Multiplexer #(.select(4), .width(4), .enable("false")) multiplexer_1 (
    .in0(4'b1111), .in1(4'b1111), .in2(CHRONO_1_u_h_chrono), .in3(MINUTEUR_1_u_h_timer), .in4(4'b1111),
    .in5(4'b1111), .in6(4'b0000), .in7(4'b0000), .in8(4'b0000), .in9(4'b0000), .in10(4'b0000),
    .in11(4'b0000), .in12(4'b0000), .in13(4'b0000), .in14(4'b0000), .in15(4'b0000), .out(multiplexer_1_out),
    .sel(mode_1_mode));
  Counter #(.width(11), .max('h7ff)) counter_1 (
    .clr(DipSwitch_1_sw10), .load(1'b0), .up(1'b1), .count(1'b1), .clk(clock_1_out), .D({11{1'b0}}),
    .carry(counter_1_carry));  // open: Q
  affich affich_2 (
    .a0(multiplexer_1_out[3]), .b0(multiplexer_1_out[2]), .c0(multiplexer_1_out[1]),
    .d0(multiplexer_1_out[0]), .a(affich_2_a), .b(affich_2_b), .c(affich_2_c), .d(affich_2_d),
    .e(affich_2_e), .f(affich_2_f), .g(affich_2_g));
  _7_Segment_Display L_7_Segment_Display_2 (
    .g(affich_2_g), .f(affich_2_f), .a(affich_2_a), .b(affich_2_b), .e(affich_2_e), .d(affich_2_d),
    .c(affich_2_c), .dp(1'b0));
  Multiplexer #(.select(4), .width(4), .enable("false")) multiplexer_2 (
    .in0(HEURE_1_d_h_now), .in1(ALARME_1_d_h_set_alarm), .in2(CHRONO_1_d_min_chrono),
    .in3(MINUTEUR_1_d_min_timer), .in4(JEUSWITCH_1_d_point), .in5(JEUMEMORY_1_d_point), .in6(4'b0000),
    .in7(4'b0000), .in8(4'b0000), .in9(4'b0000), .in10(4'b0000), .in11(4'b0000), .in12(4'b0000),
    .in13(4'b0000), .in14(4'b0000), .in15(4'b0000), .out(multiplexer_2_out), .sel(mode_1_mode));
  HEURE HEURE_1 (
    .ME(demultiplexer_1_out0), .Clock(clock_1_out), .Reset(DipSwitch_1_sw10), .Set_BTN(ButtonDeb_2_s),
    .CHA(CHA), .CHB(CHB), .Mode_Set_BTN(ButtonspeDeb_s), .U_min_Now(HEURE_1_u_min_now),
    .D_min_Now(HEURE_1_d_min_now), .U_h_Now(HEURE_1_u_h_now), .D_h_Now(HEURE_1_d_h_now),
    .Set_OK(HEURE_1_set_ok));
  ALARME ALARME_1 (
    .ME(demultiplexer_1_out1), .Set_Btn(ButtonDeb_2_s), .Reset(DipSwitch_1_sw10), .Clock(clock_1_out),
    .CHA(CHA), .CHB(CHB), .Mode_set_BTN(ButtonspeDeb_s), .ONOFF(DipSwitch_1_sw1),
    .U_min_Now(HEURE_1_u_min_now), .D_min_Now(HEURE_1_d_min_now), .U_h_Now(HEURE_1_u_h_now),
    .D_h_Now(HEURE_1_d_h_now), .D_h_set_alarm(ALARME_1_d_h_set_alarm),
    .U_h_set_alarm(ALARME_1_u_h_set_alarm), .D_min_set_alarm(ALARME_1_d_min_set_alarm),
    .U_min_set_alarm(ALARME_1_u_min_set_alarm), .Buzz(ALARME_1_buzz), .Set_OK(ALARME_1_set_ok));
  CHRONO CHRONO_1 (
    .Clock(clock_1_out), .ME(demultiplexer_1_out2), .Start_Stop(ButtonDeb_2_s),
    .Reset_chrono(ButtonspeDeb_s), .U_sec_chrono(CHRONO_1_u_sec_chrono),
    .D_sec_chrono(CHRONO_1_d_sec_chrono), .U_min_chrono(CHRONO_1_u_min_chrono),
    .D_min_chrono(CHRONO_1_d_min_chrono), .U_h_chrono(CHRONO_1_u_h_chrono));
  JEUREFLEXE JEUSWITCH_1 (
    .ME(demultiplexer_1_out4[0]), .DS1(DipSwitch_1_sw9[7]), .DS2(DipSwitch_1_sw9[6]),
    .DS3(DipSwitch_1_sw9[5]), .DS4(DipSwitch_1_sw9[4]), .DS5(DipSwitch_1_sw9[3]), .DS6(DipSwitch_1_sw9[2]),
    .DS7(DipSwitch_1_sw9[1]), .DS8(DipSwitch_1_sw9[0]), .ResetGame(ButtonspeDeb_s),
    .ResetTot(DipSwitch_1_sw10), .StartBTN(ButtonDeb_2_s), .Clock(clock_1_out), .LED1(JEUSWITCH_1_led1),
    .LED2(JEUSWITCH_1_led2), .LED3(JEUSWITCH_1_led3), .LED4(JEUSWITCH_1_led4), .LED5(JEUSWITCH_1_led5),
    .LED6(JEUSWITCH_1_led6), .LED7(JEUSWITCH_1_led7), .LED8(JEUSWITCH_1_led8), .U_point(JEUSWITCH_1_u_point),
    .D_point(JEUSWITCH_1_d_point), .U_sec_jeu(JEUSWITCH_1_u_sec_jeu), .D_sec_jeu(JEUSWITCH_1_d_sec_jeu));
  or or_1 (or_1_out, ButtonspeDeb_s, DipSwitch_1_sw10);
  MINUTEUR MINUTEUR_1 (
    .ME(demultiplexer_1_out3), .Mode_set_Start_BTN(ButtonspeDeb_s), .Set_BTN(ButtonDeb_2_s), .CHA(CHA),
    .CHB(CHB), .Reset(DipSwitch_1_sw10), .Clock(clock_1_out), .U_h_Timer(MINUTEUR_1_u_h_timer),
    .D_min_Timer(MINUTEUR_1_d_min_timer), .U_min_Timer(MINUTEUR_1_u_min_timer),
    .D_sec_Timer(MINUTEUR_1_d_sec_timer), .U_sec_Timer(MINUTEUR_1_u_sec_timer), .Buzz(MINUTEUR_1_buzz),
    .Set_OK(MINUTEUR_1_set_ok));
  affich affich_3 (
    .a0(multiplexer_2_out[3]), .b0(multiplexer_2_out[2]), .c0(multiplexer_2_out[1]),
    .d0(multiplexer_2_out[0]), .a(affich_3_a), .b(affich_3_b), .c(affich_3_c), .d(affich_3_d),
    .e(affich_3_e), .f(affich_3_f), .g(affich_3_g));
  _7_Segment_Display L_7_Segment_Display_3 (
    .g(affich_3_g), .f(affich_3_f), .a(affich_3_a), .b(affich_3_b), .e(affich_3_e), .d(affich_3_d),
    .c(affich_3_c), .dp(1'b0));
  Multiplexer #(.select(4), .width(4), .enable("false")) multiplexer_3 (
    .in0(HEURE_1_u_h_now), .in1(ALARME_1_u_h_set_alarm), .in2(CHRONO_1_u_min_chrono),
    .in3(MINUTEUR_1_u_min_timer), .in4(JEUSWITCH_1_u_point), .in5(JEUMEMORY_1_u_point), .in6(4'b0000),
    .in7(4'b0000), .in8(4'b0000), .in9(4'b0000), .in10(4'b0000), .in11(4'b0000), .in12(4'b0000),
    .in13(4'b0000), .in14(4'b0000), .in15(4'b0000), .out(multiplexer_3_out), .sel(mode_1_mode));
  JEUMEMORY JEUMEMORY_1 (
    .ME(demultiplexer_1_out4[1]), .Switch(DipSwitch_1_sw9), .Reset(or_1_out), .Clock1HZ(counter_1_carry),
    .Clock(clock_1_out), .LED1(JEUMEMORY_1_led1), .LED2(JEUMEMORY_1_led2), .LED3(JEUMEMORY_1_led3),
    .LED4(JEUMEMORY_1_led4), .LED5(JEUMEMORY_1_led5), .LED6(JEUMEMORY_1_led6), .LED7(JEUMEMORY_1_led7),
    .LED8(JEUMEMORY_1_led8), .TPS(JEUMEMORY_1_tps), .U_Point(JEUMEMORY_1_u_point),
    .D_Point(JEUMEMORY_1_d_point));
  affich affich_4 (
    .a0(multiplexer_3_out[3]), .b0(multiplexer_3_out[2]), .c0(multiplexer_3_out[1]),
    .d0(multiplexer_3_out[0]), .a(affich_4_a), .b(affich_4_b), .c(affich_4_c), .d(affich_4_d),
    .e(affich_4_e), .f(affich_4_f), .g(affich_4_g));
  _7_Segment_Display L_7_Segment_Display_4 (
    .g(affich_4_g), .f(affich_4_f), .a(affich_4_a), .b(affich_4_b), .e(affich_4_e), .d(affich_4_d),
    .c(affich_4_c), .dp(1'b0));
  Multiplexer #(.select(4), .width(4), .enable("false")) multiplexer_4 (
    .in0(HEURE_1_d_min_now), .in1(ALARME_1_d_min_set_alarm), .in2(CHRONO_1_d_sec_chrono),
    .in3(MINUTEUR_1_d_sec_timer), .in4(JEUSWITCH_1_d_sec_jeu), .in5(4'b1111), .in6(4'b0000), .in7(4'b0000),
    .in8(4'b0000), .in9(4'b0000), .in10(4'b0000), .in11(4'b0000), .in12(4'b0000), .in13(4'b0000),
    .in14(4'b0000), .in15(4'b0000), .out(multiplexer_4_out), .sel(mode_1_mode));
  affich affich_5 (
    .a0(multiplexer_4_out[3]), .b0(multiplexer_4_out[2]), .c0(multiplexer_4_out[1]),
    .d0(multiplexer_4_out[0]), .a(affich_5_a), .b(affich_5_b), .c(affich_5_c), .d(affich_5_d),
    .e(affich_5_e), .f(affich_5_f), .g(affich_5_g));
  _7_Segment_Display L_7_Segment_Display_5 (
    .g(affich_5_g), .f(affich_5_f), .a(affich_5_a), .b(affich_5_b), .e(affich_5_e), .d(affich_5_d),
    .c(affich_5_c), .dp(1'b0));
  Multiplexer #(.select(4), .width(4), .enable("false")) multiplexer_5 (
    .in0(HEURE_1_u_min_now), .in1(ALARME_1_u_min_set_alarm), .in2(CHRONO_1_u_sec_chrono),
    .in3(MINUTEUR_1_u_sec_timer), .in4(JEUSWITCH_1_u_sec_jeu), .in5(JEUMEMORY_1_tps), .in6(4'b0000),
    .in7(4'b0000), .in8(4'b0000), .in9(4'b0000), .in10(4'b0000), .in11(4'b0000), .in12(4'b0000),
    .in13(4'b0000), .in14(4'b0000), .in15(4'b0000), .out(multiplexer_5_out), .sel(mode_1_mode));
  affich affich_6 (
    .a0(multiplexer_5_out[3]), .b0(multiplexer_5_out[2]), .c0(multiplexer_5_out[1]),
    .d0(multiplexer_5_out[0]), .a(affich_6_a), .b(affich_6_b), .c(affich_6_c), .d(affich_6_d),
    .e(affich_6_e), .f(affich_6_f), .g(affich_6_g));
  _7_Segment_Display L_7_Segment_Display_6 (
    .g(affich_6_g), .f(affich_6_f), .a(affich_6_a), .b(affich_6_b), .e(affich_6_e), .d(affich_6_d),
    .c(affich_6_c), .dp(1'b0));
  or or_2 (or_2_out, HEURE_1_set_ok, ALARME_1_set_ok, MINUTEUR_1_set_ok);
  or or_3 (or_3_out, ALARME_1_buzz, MINUTEUR_1_buzz);
  and and_1 (and_1_out, clock_1_out, ~or_2_out, or_3_out);  // AND_Gate
  Counter #(.width(11), .max('h7ff)) counter_2 (
    .clr(DipSwitch_1_sw10), .load(1'b0), .up(1'b1), .count(1'b1), .clk(clock_1_out), .D({11{1'b0}}),
    .carry(counter_2_carry), .Q(counter_2_q));
  Counter #(.width(9), .max('h1ff)) counter_3 (
    .clr(DipSwitch_1_sw10), .load(1'b0), .up(1'b1), .count(1'b1), .clk(clock_1_out), .D({9{1'b0}}),
    .carry(counter_3_carry), .Q(counter_3_q));
  S_R_Flip_Flop s_r_ff_1 (
    .S(1'b0), .R(1'b0), .clk(1'b0), .Q(s_r_ff_1_q), .reset(comparator_1_eq), .preset(counter_2_carry));  // open: Qn
  Comparator #(.width(11)) comparator_1 (.a(counter_2_q), .b(11'h400), .eq(comparator_1_eq));  // open: gt, lt
  and and_2 (and_2_out, s_r_ff_1_q, and_1_out);
  S_R_Flip_Flop s_r_ff_2 (
    .S(1'b0), .R(1'b0), .clk(1'b0), .Q(s_r_ff_2_q), .reset(comparator_2_eq), .preset(counter_3_carry));  // open: Qn
  Comparator #(.width(9)) comparator_2 (.a(counter_3_q), .b(9'h100), .eq(comparator_2_eq));  // open: gt, lt
  or or_4 (or_4_out, ~or_3_out, DipSwitch_1_sw10);  // OR_Gate
  Buzzerie Buzzerie_1 (.Reset(DipSwitch_1_sw10), .Clock(and_2_out), .Buzzer(Buzzer));
  Anim_LED Anim_LED_1 (
    .Reset(or_4_out), .Clock(s_r_ff_2_q), .Buzz_ON(or_3_out), .LEDR9(Anim_LED_1_ledr9),
    .LEDR8(Anim_LED_1_ledr8), .LEDR7(Anim_LED_1_ledr7), .LEDR6(Anim_LED_1_ledr6), .LEDR5(Anim_LED_1_ledr5),
    .LEDR4(Anim_LED_1_ledr4), .LEDR3(Anim_LED_1_ledr3), .LEDR2(Anim_LED_1_ledr2), .LEDR1(Anim_LED_1_ledr1));
  Multiplexer #(.select(2), .enable("false")) multiplexer_6 (
    .in0(Anim_LED_1_ledr8), .in1(JEUSWITCH_1_led8), .in2(JEUMEMORY_1_led8), .in3(1'b0),
    .out(multiplexer_6_out), .sel(demultiplexer_1_out4));
  Multiplexer #(.select(2), .enable("false")) multiplexer_7 (
    .in0(Anim_LED_1_ledr7), .in1(JEUSWITCH_1_led7), .in2(JEUMEMORY_1_led7), .in3(1'b0),
    .out(multiplexer_7_out), .sel(demultiplexer_1_out4));
  Multiplexer #(.select(2), .enable("false")) multiplexer_8 (
    .in0(Anim_LED_1_ledr6), .in1(JEUSWITCH_1_led6), .in2(JEUMEMORY_1_led6), .in3(1'b0),
    .out(multiplexer_8_out), .sel(demultiplexer_1_out4));
  Multiplexer #(.select(2), .enable("false")) multiplexer_9 (
    .in0(Anim_LED_1_ledr5), .in1(JEUSWITCH_1_led5), .in2(JEUMEMORY_1_led5), .in3(1'b0),
    .out(multiplexer_9_out), .sel(demultiplexer_1_out4));
  Multiplexer #(.select(2), .enable("false")) multiplexer_10 (
    .in0(Anim_LED_1_ledr4), .in1(JEUSWITCH_1_led4), .in2(JEUMEMORY_1_led4), .in3(1'b0),
    .out(multiplexer_10_out), .sel(demultiplexer_1_out4));
  Multiplexer #(.select(2), .enable("false")) multiplexer_11 (
    .in0(Anim_LED_1_ledr3), .in1(JEUSWITCH_1_led3), .in2(JEUMEMORY_1_led3), .in3(1'b0),
    .out(multiplexer_11_out), .sel(demultiplexer_1_out4));
  Multiplexer #(.select(2), .enable("false")) multiplexer_12 (
    .in0(Anim_LED_1_ledr2), .in1(JEUSWITCH_1_led2), .in2(JEUMEMORY_1_led2), .in3(1'b0),
    .out(multiplexer_12_out), .sel(demultiplexer_1_out4));
  Multiplexer #(.select(2), .enable("false")) multiplexer_13 (
    .in0(Anim_LED_1_ledr1), .in1(JEUSWITCH_1_led1), .in2(JEUMEMORY_1_led1), .in3(1'b0),
    .out(multiplexer_13_out), .sel(demultiplexer_1_out4));
  LED LEDR9 (.in(Anim_LED_1_ledr9));
  LED LEDR8 (.in(multiplexer_6_out));
  LED LEDR7 (.in(multiplexer_7_out));
  LED LEDR6 (.in(multiplexer_8_out));
  LED LEDR5 (.in(multiplexer_9_out));
  LED LEDR4 (.in(multiplexer_10_out));
  LED LEDR3 (.in(multiplexer_11_out));
  LED LEDR2 (.in(multiplexer_12_out));
  LED LEDR1 (.in(multiplexer_13_out));
  LED LEDR0 (.in(DipSwitch_1_sw1));

  assign GND = 1'b0;
  assign VDD = 1'b1;

  // Notes on the sheet:
  //   1 = ON_OFF
  //   Channel C sur 1 lorsque pas d'appui
  //   10 = Reset
endmodule

module HEURE (
  input  ME,
  input  Clock,
  input  Reset,
  input  Set_BTN,
  input  CHA,
  input  CHB,
  input  Mode_Set_BTN,
  output [3:0] U_min_Now,
  output [3:0] D_min_Now,
  output [3:0] U_h_Now,
  output [3:0] D_h_Now,
  output Set_OK
);

  wire and_1_out, and_2_out, and_3_out, and_4_out, comparator_1_eq, counter_1_carry, s_r_ff_1_q;
  wire [3:0] TimeSet2_1_d_h_set, TimeSet2_1_d_min_set, TimeSet2_1_u_h_set, TimeSet2_1_u_min_set;
  wire [10:0] counter_1_q;

  and and_1 (and_1_out, ME, CHB);
  and and_2 (and_2_out, ME, Mode_Set_BTN);
  Counter #(.width(11), .max('h7ff)) counter_1 (
    .clr(Reset), .load(1'b0), .up(1'b1), .count(1'b1), .clk(Clock), .D({11{1'b0}}), .carry(counter_1_carry),
    .Q(counter_1_q));
  and and_3 (and_3_out, ME, Set_BTN);
  and and_4 (and_4_out, ME, CHA);
  Time_Set TimeSet2_1 (
    .Set_BTN(and_3_out), .Clock(Clock), .Reset(Reset), .CHA(and_4_out), .CHB(and_1_out),
    .Mode_Set_Btn(and_2_out), .D_h_set(TimeSet2_1_d_h_set), .U_h_set(TimeSet2_1_u_h_set),
    .D_min_set(TimeSet2_1_d_min_set), .U_min_set(TimeSet2_1_u_min_set), .Set_OK(Set_OK));
  S_R_Flip_Flop s_r_ff_1 (
    .S(1'b0), .R(1'b0), .clk(1'b0), .Q(s_r_ff_1_q), .reset(comparator_1_eq), .preset(counter_1_carry));  // open: Qn
  Comparator #(.width(11)) comparator_1 (.a(counter_1_q), .b(11'h400), .eq(comparator_1_eq));  // open: gt, lt
  COMPTEUR COMPTEUR_12 (
    .Clock(s_r_ff_1_q), .Reset(Reset), .Trigger(1'b1), .D_h_set(TimeSet2_1_d_h_set),
    .U_h_set(TimeSet2_1_u_h_set), .D_min_set(TimeSet2_1_d_min_set), .U_min_set(TimeSet2_1_u_min_set),
    .D_sec_set(4'b0000), .U_sec_set(4'b0000), .SET_OK(Set_OK), .U_min_Now(U_min_Now), .D_min_Now(D_min_Now),
    .U_h_Now(U_h_Now), .D_h_Now(D_h_Now));  // open: U_sec_Now, D_sec_Now
endmodule

module ALARME (
  input  ME,
  input  Set_Btn,
  input  Reset,
  input  Clock,
  input  CHA,
  input  CHB,
  input  Mode_set_BTN,
  input  ONOFF,
  input  [3:0] U_min_Now,
  input  [3:0] D_min_Now,
  input  [3:0] U_h_Now,
  input  [3:0] D_h_Now,
  output [3:0] D_h_set_alarm,
  output [3:0] U_h_set_alarm,
  output [3:0] D_min_set_alarm,
  output [3:0] U_min_set_alarm,
  output Buzz,
  output Set_OK
);

  wire and_1_out, and_2_out;

  and and_1 (and_1_out, ME, Set_Btn);
  and and_2 (and_2_out, ME, Mode_set_BTN);
  AlarmRing AlarmRing_1 (
    .ONOFF(ONOFF), .U_min_set(U_min_set_alarm), .U_min_Now(U_min_Now), .D_min_set(D_min_set_alarm),
    .D_min_Now(D_min_Now), .U_h_set(U_h_set_alarm), .U_h_Now(U_h_Now), .D_h_set(D_h_set_alarm),
    .D_h_Now(D_h_Now), .EnRing(Buzz));
  Time_Set TimeSet2_1 (
    .Set_BTN(and_1_out), .Clock(Clock), .Reset(Reset), .CHA(CHA), .CHB(CHB), .Mode_Set_Btn(and_2_out),
    .D_h_set(D_h_set_alarm), .U_h_set(U_h_set_alarm), .D_min_set(D_min_set_alarm),
    .U_min_set(U_min_set_alarm), .Set_OK(Set_OK));
endmodule

module Time_Set (
  input  Set_BTN,
  input  Clock,
  input  Reset,
  input  CHA,
  input  CHB,
  input  Mode_Set_Btn,
  output [3:0] D_h_set,
  output [3:0] U_h_set,
  output [3:0] D_min_set,
  output [3:0] U_min_set,
  output Set_OK
);

  wire and_1_out, and_2_out, and_3_out, and_4_out, and_5_out, ButtonDeb_6_s, ButtonDeb_7_s,
       comp_d_h_31_vingtaine, comp_u_h_31_anti_vingtaine, comparator_1_eq, comparator_2_eq, comparator_3_eq,
       comparator_4_eq, comparator_5_eq, counter_1_carry, DECODEURCPTL2_6_cw, demultiplexer_1_out0,
       demultiplexer_1_out1, demultiplexer_1_out2, demultiplexer_1_out3, not_1_out, not_2_out, s_r_ff_1_q;
  wire [1:0] modeTimeSet_8_modetimeset;
  wire [3:0] comp_d_h_31_o, comp_d_sec_m_31_o, comp_u_h_31_o, comp_u_sec_m_31_o;
  wire [10:0] counter_1_q;

  Counter #(.width(11), .max('h400)) counter_1 (
    .clr(Reset), .load(1'b0), .up(1'b1), .count(1'b1), .clk(Clock), .D({11{1'b0}}), .carry(counter_1_carry),
    .Q(counter_1_q));
  not not_1 (not_1_out, Set_BTN);
  S_R_Flip_Flop s_r_ff_1 (
    .S(1'b0), .R(1'b0), .clk(1'b0), .Q(s_r_ff_1_q), .reset(comparator_1_eq), .preset(counter_1_carry));  // open: Qn
  Comparator #(.width(11)) comparator_1 (.a(counter_1_q), .b(11'h200), .eq(comparator_1_eq));  // open: gt, lt
  Multiplexer #(.width(4), .enable("false")) multiplexer_1 (
    .in0(comp_d_h_31_o), .in1(4'b1111), .out(D_h_set), .sel(and_1_out));
  ButtonDeb ButtonDeb_7 (.E(not_1_out), .Clock(Clock), .Reset(Reset), .S(ButtonDeb_7_s));
  not not_2 (not_2_out, Set_OK);
  SetSwitch SetBTNSwitch_2 (.Set_Btn(ButtonDeb_7_s), .Set_Ok_mode(Set_OK));
  ButtonDeb ButtonDeb_6 (.E(Mode_Set_Btn), .Clock(Clock), .Reset(Reset), .S(ButtonDeb_6_s));
  compt_d_h comp_d_h_31 (
    .Trigger(1'b1), .Clock(demultiplexer_1_out3), .Reset(Reset), .Anti_vingtaine(comp_u_h_31_anti_vingtaine),
    .D_h_set(4'b0000), .SET_OK(1'b0), .O(comp_d_h_31_o), .Vingtaine(comp_d_h_31_vingtaine));
  DECODEURCPTL DECODEURCPTL2_6 (
    .Reset(not_2_out), .CHA(CHA), .CHB(CHB), .Clock(Clock), .CW(DECODEURCPTL2_6_cw));  // open: CCW, en_cnt
  Comparator #(.width(2)) comparator_2 (
    .a(modeTimeSet_8_modetimeset), .b(2'b11), .eq(comparator_2_eq));  // open: gt, lt
  and and_1 (and_1_out, s_r_ff_1_q, Set_OK, comparator_2_eq);
  Multiplexer #(.width(4), .enable("false")) multiplexer_2 (
    .in0(comp_u_h_31_o), .in1(4'b1111), .out(U_h_set), .sel(and_3_out));
  and and_2 (and_2_out, Set_OK, ButtonDeb_6_s);
  Comparator #(.width(2)) comparator_3 (
    .a(modeTimeSet_8_modetimeset), .b(2'b10), .eq(comparator_3_eq));  // open: gt, lt
  and and_3 (and_3_out, s_r_ff_1_q, Set_OK, comparator_3_eq);
  compt_u_h comp_u_h_31 (
    .Vingtaine(comp_d_h_31_vingtaine), .Trigger(1'b1), .Clock(demultiplexer_1_out2), .Reset(Reset),
    .U_h_set(4'b0000), .SET_OK(1'b0), .O(comp_u_h_31_o), .Anti_Vingtaine(comp_u_h_31_anti_vingtaine));  // open: Retenu
  Comparator #(.width(2)) comparator_4 (
    .a(modeTimeSet_8_modetimeset), .b(2'b01), .eq(comparator_4_eq));  // open: gt, lt
  and and_4 (and_4_out, s_r_ff_1_q, Set_OK, comparator_4_eq);
  Demultiplexer #(.select(2), .enable("false")) demultiplexer_1 (
    .out0(demultiplexer_1_out0), .out1(demultiplexer_1_out1), .out2(demultiplexer_1_out2),
    .out3(demultiplexer_1_out3), .in(DECODEURCPTL2_6_cw), .sel(modeTimeSet_8_modetimeset));
  Multiplexer #(.width(4), .enable("false")) multiplexer_3 (
    .in0(comp_d_sec_m_31_o), .in1(4'b1111), .out(D_min_set), .sel(and_4_out));
  modeTimeSet_twoB modeTimeSet_8 (
    .Set_BTN(and_2_out), .Clock(Clock), .Reset(Reset), .ModeTimeSet(modeTimeSet_8_modetimeset));
  and and_5 (and_5_out, s_r_ff_1_q, Set_OK, comparator_5_eq);
  comp_d_sec_m comp_d_sec_m_31 (
    .Trigger(1'b1), .Clock(demultiplexer_1_out1), .Reset(Reset), .D_sec_m_set(4'b0000), .SET_OK(1'b0),
    .O(comp_d_sec_m_31_o));  // open: Retenu
  Comparator #(.width(2)) comparator_5 (
    .a(modeTimeSet_8_modetimeset), .b(2'b00), .eq(comparator_5_eq));  // open: gt, lt
  Multiplexer #(.width(4), .enable("false")) multiplexer_4 (
    .in0(comp_u_sec_m_31_o), .in1(4'b1111), .out(U_min_set), .sel(and_5_out));
  compt_u_sec_m comp_u_sec_m_31 (
    .Trigger(1'b1), .Clock(demultiplexer_1_out0), .Reset(Reset), .U_sec_m_set(4'b0000), .SET_OK(1'b0),
    .O(comp_u_sec_m_31_o));  // open: Retenu
endmodule

module AlarmRing (
  input  ONOFF,
  input  [3:0] U_min_set,
  input  [3:0] U_min_Now,
  input  [3:0] D_min_set,
  input  [3:0] D_min_Now,
  input  [3:0] U_h_set,
  input  [3:0] U_h_Now,
  input  [3:0] D_h_set,
  input  [3:0] D_h_Now,
  output EnRing
);

  wire and_1_out, comparator_1_eq, comparator_2_eq, comparator_3_eq, comparator_4_eq;

  Comparator #(.width(4)) comparator_1 (.a(U_min_set), .b(U_min_Now), .eq(comparator_1_eq));  // open: gt, lt
  Comparator #(.width(4)) comparator_2 (.a(D_min_set), .b(D_min_Now), .eq(comparator_2_eq));  // open: gt, lt
  Comparator #(.width(4)) comparator_3 (.a(U_h_set), .b(U_h_Now), .eq(comparator_3_eq));  // open: gt, lt
  Comparator #(.width(4)) comparator_4 (.a(D_h_set), .b(D_h_Now), .eq(comparator_4_eq));  // open: gt, lt
  and and_1 (and_1_out, comparator_1_eq, comparator_2_eq, comparator_3_eq, comparator_4_eq);
  and and_2 (EnRing, ONOFF, and_1_out);
endmodule

module modeTimeSet_twoB (
  input  Set_BTN,
  input  Clock,
  input  Reset,
  output [1:0] ModeTimeSet
);

  wire comparator_1_lt;
  wire [1:0] adder_1_out, bit_extender_1_out, multiplexer_1_out;

  assign bit_extender_1_out = {{1{1'b0}}, Set_BTN};  // Bit_Extender bit_extender_1
  Adder #(.width(2)) adder_1 (
    .a(multiplexer_1_out), .b(bit_extender_1_out), .out(adder_1_out), .cin(1'b0));  // open: cout
  D_Flip_Flop d_ff_1 (.D(adder_1_out[1]), .clk(Clock), .Q(ModeTimeSet[1]), .preset(1'b0), .reset(Reset));  // open: Qn
  D_Flip_Flop d_ff_2 (.D(adder_1_out[0]), .clk(Clock), .Q(ModeTimeSet[0]), .preset(1'b0), .reset(Reset));  // open: Qn
  Multiplexer #(.width(2), .enable("false")) multiplexer_1 (
    .in0(2'b00), .in1(ModeTimeSet), .out(multiplexer_1_out), .sel(comparator_1_lt));
  Comparator #(.width(2), .mode("unsigned")) comparator_1 (
    .a(2'b00), .b(ModeTimeSet), .lt(comparator_1_lt));  // open: gt, eq
endmodule

module CHRONO (
  input  Clock,
  input  ME,
  input  Start_Stop,
  input  Reset_chrono,
  output [3:0] U_sec_chrono,
  output [3:0] D_sec_chrono,
  output [3:0] U_min_chrono,
  output [3:0] D_min_chrono,
  output [3:0] U_h_chrono
);

  wire and_1_out, comparator_1_eq, counter_1_carry, s_r_ff_1_q, SetSwitch_2_set_ok_mode;
  wire [10:0] counter_1_q;

  and and_1 (and_1_out, ME, Start_Stop);
  SetSwitch SetSwitch_2 (.Set_Btn(and_1_out), .Set_Ok_mode(SetSwitch_2_set_ok_mode));
  Counter #(.width(11), .max('hfff)) counter_1 (
    .clr(Reset_chrono), .load(1'b0), .up(1'b1), .count(1'b1), .clk(Clock), .D({11{1'b0}}),
    .carry(counter_1_carry), .Q(counter_1_q));
  S_R_Flip_Flop s_r_ff_1 (
    .S(1'b0), .R(1'b0), .clk(1'b0), .Q(s_r_ff_1_q), .reset(comparator_1_eq), .preset(counter_1_carry));  // open: Qn
  Comparator #(.width(11)) comparator_1 (.a(counter_1_q), .b(11'h400), .eq(comparator_1_eq));  // open: gt, lt
  COMPTEUR COMPTEUR_1 (
    .Clock(s_r_ff_1_q), .Reset(Reset_chrono), .Trigger(SetSwitch_2_set_ok_mode), .D_h_set(4'b0000),
    .U_h_set(4'b0000), .D_min_set(4'b0000), .U_min_set(4'b0000), .D_sec_set(4'b0000), .U_sec_set(4'b0000),
    .SET_OK(1'b0), .U_sec_Now(U_sec_chrono), .D_sec_Now(D_sec_chrono), .U_min_Now(U_min_chrono),
    .D_min_Now(D_min_chrono), .U_h_Now(U_h_chrono));  // open: D_h_Now
endmodule

module SetSwitch (
  input  Set_Btn,
  output Set_Ok_mode
);

  wire and_1_out, d_ff_1_q;

  and and_1 (and_1_out, Set_Btn, d_ff_1_q);
  S_R_Flip_Flop s_r_ff_1 (
    .S(1'b0), .R(1'b0), .clk(1'b0), .Q(Set_Ok_mode), .reset(and_1_out), .preset(Set_Btn));  // open: Qn
  D_Flip_Flop d_ff_1 (.D(Set_Ok_mode), .clk(Set_Btn), .Q(d_ff_1_q), .preset(1'b0), .reset(1'b0));  // open: Qn
endmodule

module MINUTEUR (
  input  ME,
  input  Mode_set_Start_BTN,
  input  Set_BTN,
  input  CHA,
  input  CHB,
  input  Reset,
  input  Clock,
  output [3:0] U_h_Timer,
  output [3:0] D_min_Timer,
  output [3:0] U_min_Timer,
  output [3:0] D_sec_Timer,
  output [3:0] U_sec_Timer,
  output Buzz,
  output Set_OK
);

  wire and_1_out, and_2_out, and_3_out, and_4_out, and_5_out, comparator_1_eq, comparator_2_eq,
       comparator_3_eq, comparator_4_eq, comparator_5_eq, comparator_6_eq, comparator_7_eq, comparator_8_eq,
       comparator_9_eq, comparator_10_eq, comparator_11_eq, counter_1_carry, counter_2_carry, d_ff_1_q,
       or_1_out, or_2_out, s_r_ff_1_q, SetSwitch_4_set_ok_mode;
  wire [3:0] DECOMPTEUR_1_d_min_now, DECOMPTEUR_1_d_sec_now, DECOMPTEUR_1_u_h_now, DECOMPTEUR_1_u_min_now,
       DECOMPTEUR_1_u_sec_now, SetMinuteur_1_d_min_set, SetMinuteur_1_d_sec_set, SetMinuteur_1_u_h_set,
       SetMinuteur_1_u_min_set, SetMinuteur_1_u_sec_set;
  wire [10:0] counter_1_q;

  and and_1 (and_1_out, ME, Set_BTN);
  and and_2 (and_2_out, ME, Mode_set_Start_BTN);
  and and_3 (and_3_out, ME, ~Set_OK, Mode_set_Start_BTN);  // AND_Gate
  Counter #(.width(11), .max('h7ff)) counter_1 (
    .clr(Reset), .load(1'b0), .up(1'b1), .count(1'b1), .clk(Clock), .D({11{1'b0}}), .carry(counter_1_carry),
    .Q(counter_1_q));
  SetSwitch SetSwitch_4 (.Set_Btn(and_3_out), .Set_Ok_mode(SetSwitch_4_set_ok_mode));
  SetMinuteur SetMinuteur_1 (
    .Set_BTN(and_1_out), .Reset(Reset), .Clock(Clock), .CHA(CHA), .CHB(CHB), .Mode_set_BTN(and_2_out),
    .U_h_set(SetMinuteur_1_u_h_set), .D_min_set(SetMinuteur_1_d_min_set),
    .U_min_set(SetMinuteur_1_u_min_set), .D_sec_set(SetMinuteur_1_d_sec_set),
    .U_sec_set(SetMinuteur_1_u_sec_set), .SET_OK(Set_OK));
  Counter #(.width(5), .max('h1e)) counter_2 (
    .clr(Reset), .load(1'b0), .up(1'b1), .count(1'b1), .clk(s_r_ff_1_q), .D({5{1'b0}}),
    .carry(counter_2_carry));  // open: Q
  or or_1 (or_1_out, d_ff_1_q, Reset);
  S_R_Flip_Flop s_r_ff_1 (
    .S(1'b0), .R(1'b0), .clk(1'b0), .Q(s_r_ff_1_q), .reset(comparator_1_eq), .preset(counter_1_carry));  // open: Qn
  Comparator #(.width(11)) comparator_1 (.a(counter_1_q), .b(11'h400), .eq(comparator_1_eq));  // open: gt, lt
  DECOMPTEUR DECOMPTEUR_1 (
    .Clock(s_r_ff_1_q), .Reset(or_1_out), .Trigger(SetSwitch_4_set_ok_mode), .D_h_set(4'b0000),
    .U_h_set(SetMinuteur_1_u_h_set), .D_min_set(SetMinuteur_1_d_min_set),
    .U_min_set(SetMinuteur_1_u_min_set), .D_sec_set(SetMinuteur_1_d_sec_set),
    .U_sec_set(SetMinuteur_1_u_sec_set), .SET_OK(Set_OK), .U_sec_Now(DECOMPTEUR_1_u_sec_now),
    .D_sec_Now(DECOMPTEUR_1_d_sec_now), .U_min_Now(DECOMPTEUR_1_u_min_now),
    .D_min_Now(DECOMPTEUR_1_d_min_now), .U_h_Now(DECOMPTEUR_1_u_h_now));  // open: D_h_Now
  or or_2 (or_2_out, counter_2_carry, Set_BTN);
  D_Flip_Flop d_ff_1 (.D(and_4_out), .clk(s_r_ff_1_q), .Q(d_ff_1_q), .preset(1'b0), .reset(1'b0));  // open: Qn
  D_Flip_Flop d_ff_2 (.D(1'b0), .clk(1'b0), .Q(Buzz), .preset(and_5_out), .reset(or_2_out));  // open: Qn
  Multiplexer #(.width(4), .enable("false")) multiplexer_1 (
    .in0(DECOMPTEUR_1_u_h_now), .in1(SetMinuteur_1_u_h_set), .out(U_h_Timer), .sel(Set_OK));
  Multiplexer #(.width(4), .enable("false")) multiplexer_2 (
    .in0(DECOMPTEUR_1_d_min_now), .in1(SetMinuteur_1_d_min_set), .out(D_min_Timer), .sel(Set_OK));
  Multiplexer #(.width(4), .enable("false")) multiplexer_3 (
    .in0(DECOMPTEUR_1_u_min_now), .in1(SetMinuteur_1_u_min_set), .out(U_min_Timer), .sel(Set_OK));
  Multiplexer #(.width(4), .enable("false")) multiplexer_4 (
    .in0(DECOMPTEUR_1_d_sec_now), .in1(SetMinuteur_1_d_sec_set), .out(D_sec_Timer), .sel(Set_OK));
  Multiplexer #(.width(4), .enable("false")) multiplexer_5 (
    .in0(DECOMPTEUR_1_u_sec_now), .in1(SetMinuteur_1_u_sec_set), .out(U_sec_Timer), .sel(Set_OK));
  Comparator #(.width(4)) comparator_2 (.a(U_h_Timer), .b(4'b0000), .eq(comparator_2_eq));  // open: gt, lt
  Comparator #(.width(4)) comparator_3 (.a(D_min_Timer), .b(4'b0000), .eq(comparator_3_eq));  // open: gt, lt
  Comparator #(.width(4)) comparator_4 (.a(U_min_Timer), .b(4'b0000), .eq(comparator_4_eq));  // open: gt, lt
  Comparator #(.width(4)) comparator_5 (.a(D_sec_Timer), .b(4'b0000), .eq(comparator_5_eq));  // open: gt, lt
  Comparator #(.width(4)) comparator_6 (.a(U_sec_Timer), .b(4'b0000), .eq(comparator_6_eq));  // open: gt, lt
  Comparator #(.width(4)) comparator_7 (.a(U_h_Timer), .b(4'b0000), .eq(comparator_7_eq));  // open: gt, lt
  Comparator #(.width(4)) comparator_8 (.a(D_min_Timer), .b(4'b0000), .eq(comparator_8_eq));  // open: gt, lt
  Comparator #(.width(4)) comparator_9 (.a(U_min_Timer), .b(4'b0000), .eq(comparator_9_eq));  // open: gt, lt
  Comparator #(.width(4)) comparator_10 (.a(D_sec_Timer), .b(4'b0000), .eq(comparator_10_eq));  // open: gt, lt
  Comparator #(.width(4)) comparator_11 (.a(U_sec_Timer), .b(4'b0001), .eq(comparator_11_eq));  // open: gt, lt
  and and_4 (and_4_out, comparator_2_eq, comparator_3_eq, comparator_4_eq, comparator_5_eq, comparator_6_eq);
  and and_5 (and_5_out, comparator_7_eq, comparator_8_eq, comparator_9_eq, comparator_10_eq, comparator_11_eq);
endmodule

module SetMinuteur (
  input  Set_BTN,
  input  Reset,
  input  Clock,
  input  CHA,
  input  CHB,
  input  Mode_set_BTN,
  output [3:0] U_h_set,
  output [3:0] D_min_set,
  output [3:0] U_min_set,
  output [3:0] D_sec_set,
  output [3:0] U_sec_set,
  output SET_OK
);

  wire and_1_out, and_2_out, and_3_out, and_4_out, and_5_out, and_6_out, ButtonDeb_5_s, ButtonDeb_6_s,
       comparator_1_eq, comparator_2_eq, comparator_3_eq, comparator_4_eq, comparator_5_eq, comparator_6_eq,
       counter_1_carry, DECODEURCPTL2_2_cw, demultiplexer_1_out0, demultiplexer_1_out1, demultiplexer_1_out2,
       demultiplexer_1_out3, demultiplexer_1_out4, not_1_out, s_r_ff_1_q;
  wire [2:0] modeTimeSet_threeB_1_modetimeset;
  wire [3:0] comp_d_sec_m_21_o, comp_d_sec_m_22_o, compt_u_h_2_o, compt_u_sec_m_21_o, compt_u_sec_m_22_o;
  wire [10:0] counter_1_q;

  Counter #(.width(11), .max('h400)) counter_1 (
    .clr(Reset), .load(1'b0), .up(1'b1), .count(1'b1), .clk(Clock), .D({11{1'b0}}), .carry(counter_1_carry),
    .Q(counter_1_q));
  S_R_Flip_Flop s_r_ff_1 (
    .S(1'b0), .R(1'b0), .clk(1'b0), .Q(s_r_ff_1_q), .reset(comparator_1_eq), .preset(counter_1_carry));  // open: Qn
  Comparator #(.width(11)) comparator_1 (.a(counter_1_q), .b(11'h200), .eq(comparator_1_eq));  // open: gt, lt
  Multiplexer #(.width(4), .enable("false")) multiplexer_1 (
    .in0(compt_u_h_2_o), .in1(4'b1111), .out(U_h_set), .sel(and_1_out));
  ButtonDeb ButtonDeb_5 (.E(Set_BTN), .Clock(Clock), .Reset(Reset), .S(ButtonDeb_5_s));
  not not_1 (not_1_out, SET_OK);
  SetSwitch SetSwitch_3 (.Set_Btn(ButtonDeb_5_s), .Set_Ok_mode(SET_OK));
  ButtonDeb ButtonDeb_6 (.E(Mode_set_BTN), .Clock(Clock), .Reset(Reset), .S(ButtonDeb_6_s));
  compt_u_h compt_u_h_2 (
    .Vingtaine(1'b0), .Trigger(1'b1), .Clock(demultiplexer_1_out4), .Reset(Reset), .U_h_set(4'b0000),
    .SET_OK(1'b0), .O(compt_u_h_2_o));  // open: Retenu, Anti_Vingtaine
  DECODEURCPTL DECODEURCPTL2_2 (
    .Reset(not_1_out), .CHA(CHA), .CHB(CHB), .Clock(Clock), .CW(DECODEURCPTL2_2_cw));  // open: CCW, en_cnt
  Comparator #(.width(3)) comparator_2 (
    .a(modeTimeSet_threeB_1_modetimeset), .b(3'b100), .eq(comparator_2_eq));  // open: gt, lt
  and and_1 (and_1_out, s_r_ff_1_q, SET_OK, comparator_2_eq);
  Multiplexer #(.width(4), .enable("false")) multiplexer_2 (
    .in0(comp_d_sec_m_22_o), .in1(4'b1111), .out(D_min_set), .sel(and_3_out));
  and and_2 (and_2_out, SET_OK, ButtonDeb_6_s);
  Comparator #(.width(3)) comparator_3 (
    .a(modeTimeSet_threeB_1_modetimeset), .b(3'b011), .eq(comparator_3_eq));  // open: gt, lt
  and and_3 (and_3_out, s_r_ff_1_q, SET_OK, comparator_3_eq);
  comp_d_sec_m comp_d_sec_m_22 (
    .Trigger(1'b1), .Clock(demultiplexer_1_out3), .Reset(Reset), .D_sec_m_set(4'b0000), .SET_OK(1'b0),
    .O(comp_d_sec_m_22_o));  // open: Retenu
  Multiplexer #(.width(4), .enable("false")) multiplexer_3 (
    .in0(compt_u_sec_m_22_o), .in1(4'b1111), .out(U_min_set), .sel(and_4_out));
  Comparator #(.width(3)) comparator_4 (
    .a(modeTimeSet_threeB_1_modetimeset), .b(3'b010), .eq(comparator_4_eq));  // open: gt, lt
  and and_4 (and_4_out, s_r_ff_1_q, SET_OK, comparator_4_eq);
  Demultiplexer #(.select(3), .enable("false")) demultiplexer_1 (
    .out0(demultiplexer_1_out0), .out1(demultiplexer_1_out1), .out2(demultiplexer_1_out2),
    .out3(demultiplexer_1_out3), .out4(demultiplexer_1_out4), .in(DECODEURCPTL2_2_cw),
    .sel(modeTimeSet_threeB_1_modetimeset));  // open: out5, out6, out7
  compt_u_sec_m compt_u_sec_m_22 (
    .Trigger(1'b1), .Clock(demultiplexer_1_out2), .Reset(Reset), .U_sec_m_set(4'b0000), .SET_OK(1'b0),
    .O(compt_u_sec_m_22_o));  // open: Retenu
  modeTimeSet_threeB modeTimeSet_threeB_1 (
    .Set_BTN(and_2_out), .Clock(Clock), .Reset(Reset), .ModeTimeSet(modeTimeSet_threeB_1_modetimeset));
  and and_5 (and_5_out, s_r_ff_1_q, SET_OK, comparator_5_eq);
  Comparator #(.width(3)) comparator_5 (
    .a(modeTimeSet_threeB_1_modetimeset), .b(3'b001), .eq(comparator_5_eq));  // open: gt, lt
  Multiplexer #(.width(4), .enable("false")) multiplexer_4 (
    .in0(comp_d_sec_m_21_o), .in1(4'b1111), .out(D_sec_set), .sel(and_5_out));
  and and_6 (and_6_out, s_r_ff_1_q, SET_OK, comparator_6_eq);
  comp_d_sec_m comp_d_sec_m_21 (
    .Trigger(1'b1), .Clock(demultiplexer_1_out1), .Reset(Reset), .D_sec_m_set(4'b0000), .SET_OK(1'b0),
    .O(comp_d_sec_m_21_o));  // open: Retenu
  Comparator #(.width(3)) comparator_6 (
    .a(modeTimeSet_threeB_1_modetimeset), .b(3'b000), .eq(comparator_6_eq));  // open: gt, lt
  Multiplexer #(.width(4), .enable("false")) multiplexer_5 (
    .in0(compt_u_sec_m_21_o), .in1(4'b1111), .out(U_sec_set), .sel(and_6_out));
  compt_u_sec_m compt_u_sec_m_21 (
    .Trigger(1'b1), .Clock(demultiplexer_1_out0), .Reset(Reset), .U_sec_m_set(4'b0000), .SET_OK(1'b0),
    .O(compt_u_sec_m_21_o));  // open: Retenu
endmodule

module modeTimeSet_threeB (
  input  Set_BTN,
  input  Clock,
  input  Reset,
  output [2:0] ModeTimeSet
);

  wire comparator_1_gt, comparator_2_eq, nand_1_out;
  wire [2:0] adder_1_out, bit_extender_1_out, bit_extender_2_out, d_ff_2_q, multiplexer_1_out;

  assign bit_extender_1_out = {{2{1'b0}}, Set_BTN};  // Bit_Extender bit_extender_1
  Adder #(.width(3)) adder_1 (
    .a(multiplexer_1_out), .b(bit_extender_1_out), .out(adder_1_out), .cin(1'b0));  // open: cout
  D_Flip_Flop d_ff_1 (.D(adder_1_out[1]), .clk(Clock), .Q(d_ff_2_q[1]), .preset(1'b0), .reset(Reset));  // open: Qn
  D_Flip_Flop d_ff_2 (.D(adder_1_out[0]), .clk(Clock), .Q(d_ff_2_q[0]), .preset(1'b0), .reset(Reset));  // open: Qn
  D_Flip_Flop d_ff_3 (.D(adder_1_out[2]), .clk(Clock), .Q(d_ff_2_q[2]), .preset(1'b0), .reset(Reset));  // open: Qn
  Multiplexer #(.width(3), .enable("false")) multiplexer_1 (
    .in0(3'b000), .in1(d_ff_2_q), .out(multiplexer_1_out), .sel(comparator_1_gt));
  Comparator #(.width(3), .mode("unsigned")) comparator_1 (
    .a(3'b101), .b(d_ff_2_q), .gt(comparator_1_gt));  // open: eq, lt
  Comparator #(.width(3)) comparator_2 (.a(d_ff_2_q), .b(3'b101), .eq(comparator_2_eq));  // open: gt, lt
  Multiplexer #(.width(3), .enable("false")) multiplexer_2 (
    .in0(d_ff_2_q), .in1(bit_extender_2_out), .out(ModeTimeSet), .sel(comparator_2_eq));
  nand nand_1 (nand_1_out, comparator_2_eq, 1'b1);
  assign bit_extender_2_out = {{2{nand_1_out}}, nand_1_out};  // Bit_Extender bit_extender_2
endmodule

module Anim_LED (
  input  Reset,
  input  Clock,
  input  Buzz_ON,
  output LEDR9,
  output LEDR8,
  output LEDR7,
  output LEDR6,
  output LEDR5,
  output LEDR4,
  output LEDR3,
  output LEDR2,
  output LEDR1
);

  wire and_1_out, and_2_out, and_3_out, and_4_out, and_5_out, and_6_out, and_7_out, and_8_out, and_9_out,
       and_10_out, and_11_out, and_12_out, and_13_out, and_14_out, and_15_out, and_16_out, and_17_out,
       and_18_out, and_19_out, or_1_out, or_2_out, or_3_out, or_4_out, or_5_out, or_6_out, or_7_out,
       or_8_out, or_9_out;

  and and_1 (and_1_out, Clock, Buzz_ON);
  and and_2 (and_2_out, ~and_1_out, LEDR9, LEDR8, LEDR7);  // AND_Gate
  and and_3 (and_3_out, and_1_out, ~LEDR9, ~LEDR8, ~LEDR7);  // AND_Gate
  and and_4 (and_4_out, and_1_out, ~LEDR9, LEDR8, LEDR7);  // AND_Gate
  and and_5 (and_5_out, ~and_1_out, LEDR9, ~LEDR8, ~LEDR7);  // AND_Gate
  and and_6 (and_6_out, ~and_1_out, ~LEDR9, ~LEDR8, LEDR7);  // AND_Gate
  and and_7 (and_7_out, and_1_out, LEDR9, LEDR8, ~LEDR7);  // AND_Gate
  and and_8 (and_8_out, and_1_out, ~LEDR8, ~LEDR7, LEDR6);  // AND_Gate
  and and_9 (and_9_out, ~and_1_out, LEDR8, LEDR7, ~LEDR6);  // AND_Gate
  and and_10 (and_10_out, ~and_1_out, ~LEDR7, ~LEDR6, LEDR5);  // AND_Gate
  and and_11 (and_11_out, and_1_out, LEDR7, LEDR6, ~LEDR5);  // AND_Gate
  and and_12 (and_12_out, and_1_out, ~LEDR6, ~LEDR5, LEDR4);  // AND_Gate
  and and_13 (and_13_out, ~and_1_out, LEDR6, LEDR5, ~LEDR4);  // AND_Gate
  and and_14 (and_14_out, ~and_1_out, ~LEDR5, ~LEDR4, LEDR3);  // AND_Gate
  and and_15 (and_15_out, and_1_out, LEDR5, LEDR4, ~LEDR3);  // AND_Gate
  and and_16 (and_16_out, and_1_out, ~LEDR4, ~LEDR3, LEDR2);  // AND_Gate
  and and_17 (and_17_out, ~and_1_out, LEDR4, LEDR3, ~LEDR2);  // AND_Gate
  and and_18 (and_18_out, ~and_1_out, ~LEDR3, ~LEDR2, LEDR1);  // AND_Gate
  and and_19 (and_19_out, and_1_out, LEDR3, LEDR2, ~LEDR1);  // AND_Gate
  S_R_Flip_Flop s_r_ff_1 (.S(1'b0), .R(1'b0), .clk(1'b0), .Q(LEDR9), .reset(or_1_out), .preset(and_3_out));  // open: Qn
  or or_1 (or_1_out, and_2_out, Reset);
  S_R_Flip_Flop s_r_ff_2 (.S(1'b0), .R(1'b0), .clk(1'b0), .Q(LEDR8), .reset(or_2_out), .preset(and_5_out));  // open: Qn
  or or_2 (or_2_out, and_4_out, Reset);
  S_R_Flip_Flop s_r_ff_3 (.S(1'b0), .R(1'b0), .clk(1'b0), .Q(LEDR7), .reset(or_3_out), .preset(and_7_out));  // open: Qn
  or or_3 (or_3_out, and_6_out, Reset);
  S_R_Flip_Flop s_r_ff_4 (.S(1'b0), .R(1'b0), .clk(1'b0), .Q(LEDR6), .reset(or_4_out), .preset(and_9_out));  // open: Qn
  or or_4 (or_4_out, and_8_out, Reset);
  S_R_Flip_Flop s_r_ff_5 (
    .S(1'b0), .R(1'b0), .clk(1'b0), .Q(LEDR5), .reset(or_5_out), .preset(and_11_out));  // open: Qn
  or or_5 (or_5_out, and_10_out, Reset);
  S_R_Flip_Flop s_r_ff_6 (
    .S(1'b0), .R(1'b0), .clk(1'b0), .Q(LEDR4), .reset(or_6_out), .preset(and_13_out));  // open: Qn
  or or_6 (or_6_out, and_12_out, Reset);
  S_R_Flip_Flop s_r_ff_7 (
    .S(1'b0), .R(1'b0), .clk(1'b0), .Q(LEDR3), .reset(or_7_out), .preset(and_15_out));  // open: Qn
  or or_7 (or_7_out, and_14_out, Reset);
  S_R_Flip_Flop s_r_ff_8 (
    .S(1'b0), .R(1'b0), .clk(1'b0), .Q(LEDR2), .reset(or_8_out), .preset(and_17_out));  // open: Qn
  or or_8 (or_8_out, and_16_out, Reset);
  S_R_Flip_Flop s_r_ff_9 (
    .S(1'b0), .R(1'b0), .clk(1'b0), .Q(LEDR1), .reset(or_9_out), .preset(and_19_out));  // open: Qn
  or or_9 (or_9_out, and_18_out, Reset);
endmodule

module JEUREFLEXE (
  input  ME,
  input  DS1,
  input  DS2,
  input  DS3,
  input  DS4,
  input  DS5,
  input  DS6,
  input  DS7,
  input  DS8,
  input  ResetGame,
  input  ResetTot,
  input  StartBTN,
  input  Clock,
  output LED1,
  output LED2,
  output LED3,
  output LED4,
  output LED5,
  output LED6,
  output LED7,
  output LED8,
  output [3:0] U_point,
  output [3:0] D_point,
  output [3:0] U_sec_jeu,
  output [3:0] D_sec_jeu
);

  wire and_1_out, and_2_out, and_3_out, and_4_out, and_5_out, and_6_out, and_7_out, and_8_out, and_9_out,
       and_10_out, and_11_out, and_12_out, comparator_1_eq, comparator_2_eq, comparator_3_eq,
       comparator_4_eq, comparator_5_eq, compt_PT_u_retenu, counter_1_carry, counter_2_carry, d_ff_1_q,
       jeuswitchcore_1_point, not_1_out, or_1_out, or_2_out, or_3_out, s_r_ff_1_q, s_r_ff_2_q,
       SetSwitch_jeu_set_ok_mode;
  wire [3:0] compt_PT_D_o, compt_PT_u_o;
  wire [6:0] counter_1_q;
  wire [10:0] counter_2_q;

  and and_1 (and_1_out, ME, ResetGame);
  or or_1 (or_1_out, and_1_out, ResetTot);
  and and_2 (and_2_out, ME, StartBTN);
  Counter #(.width(7), .max('h7f)) counter_1 (
    .clr(or_1_out), .load(1'b0), .up(1'b1), .count(1'b1), .clk(Clock), .D({7{1'b0}}),
    .carry(counter_1_carry), .Q(counter_1_q));
  or or_2 (or_2_out, and_2_out, and_11_out);
  Counter #(.width(11), .max('h7ff)) counter_2 (
    .clr(or_1_out), .load(1'b0), .up(1'b1), .count(1'b1), .clk(Clock), .D({11{1'b0}}),
    .carry(counter_2_carry), .Q(counter_2_q));
  S_R_Flip_Flop s_r_ff_1 (
    .S(1'b0), .R(1'b0), .clk(1'b0), .Q(s_r_ff_1_q), .reset(comparator_1_eq), .preset(counter_1_carry));  // open: Qn
  SetSwitch SetSwitch_jeu (.Set_Btn(or_2_out), .Set_Ok_mode(SetSwitch_jeu_set_ok_mode));
  and and_3 (and_3_out, ME, DS2);
  and and_4 (and_4_out, ME, DS4);
  and and_5 (and_5_out, ME, DS6);
  and and_6 (and_6_out, ME, DS8);
  Comparator #(.width(7)) comparator_1 (.a(counter_1_q), .b(7'b1000000), .eq(comparator_1_eq));  // open: gt, lt
  not not_1 (not_1_out, SetSwitch_jeu_set_ok_mode);
  S_R_Flip_Flop s_r_ff_2 (
    .S(1'b0), .R(1'b0), .clk(1'b0), .Q(s_r_ff_2_q), .reset(comparator_2_eq), .preset(counter_2_carry));  // open: Qn
  and and_7 (and_7_out, ME, DS1);
  and and_8 (and_8_out, ME, DS3);
  and and_9 (and_9_out, ME, DS5);
  and and_10 (and_10_out, ME, DS7);
  Comparator #(.width(11)) comparator_2 (.a(counter_2_q), .b(11'h400), .eq(comparator_2_eq));  // open: gt, lt
  jeuswitchcore jeuswitchcore_1 (
    .DS1(and_7_out), .DS2(and_3_out), .DS3(and_8_out), .DS4(and_4_out), .DS5(and_9_out), .DS6(and_5_out),
    .DS7(and_10_out), .DS8(and_6_out), .Clock(s_r_ff_1_q), .ClockOrigin(Clock), .Reset(or_1_out),
    .LED1(LED1), .LED2(LED2), .LED3(LED3), .LED4(LED4), .LED5(LED5), .LED6(LED6), .LED7(LED7), .LED8(LED8),
    .Point(jeuswitchcore_1_point));
  DECOMPTEUR DECOMPTEUR_Jeu (
    .Clock(s_r_ff_2_q), .Reset(or_1_out), .Trigger(ME), .D_h_set(4'b0000), .U_h_set(4'b0000),
    .D_min_set(4'b0000), .U_min_set(4'b0000), .D_sec_set(4'b0011), .U_sec_set(4'b0000), .SET_OK(not_1_out),
    .U_sec_Now(U_sec_jeu), .D_sec_Now(D_sec_jeu));  // open: U_min_Now, D_min_Now, U_h_Now, D_h_Now
  Comparator #(.width(4)) comparator_3 (.a(4'b0000), .b(U_sec_jeu), .eq(comparator_3_eq));  // open: gt, lt
  Comparator #(.width(4)) comparator_4 (.a(4'b0000), .b(D_sec_jeu), .eq(comparator_4_eq));  // open: gt, lt
  Comparator #(.width(4)) comparator_5 (.a(4'b0011), .b(D_sec_jeu), .eq(comparator_5_eq));  // open: gt, lt
  and and_11 (and_11_out, comparator_3_eq, comparator_4_eq);
  and and_12 (and_12_out, comparator_3_eq, comparator_5_eq);
  compt_u_sec_m compt_PT_u (
    .Trigger(SetSwitch_jeu_set_ok_mode), .Clock(jeuswitchcore_1_point), .Reset(or_1_out),
    .U_sec_m_set(4'b0000), .SET_OK(1'b0), .Retenu(compt_PT_u_retenu), .O(compt_PT_u_o));
  compt_u_sec_m compt_PT_D (
    .Trigger(SetSwitch_jeu_set_ok_mode), .Clock(compt_PT_u_retenu), .Reset(or_1_out), .U_sec_m_set(4'b0000),
    .SET_OK(1'b0), .O(compt_PT_D_o));  // open: Retenu
  D_Flip_Flop d_ff_1 (.D(and_12_out), .clk(Clock), .Q(d_ff_1_q), .preset(1'b0), .reset(or_1_out));  // open: Qn
  or or_3 (or_3_out, or_1_out, d_ff_1_q);
  save_score Save_score_1 (
    .U_score_in(compt_PT_u_o), .D_score_in(compt_PT_D_o), .Save_Mode(and_12_out), .Reset(or_3_out),
    .U_score_out(U_point), .D_score_out(D_point));
endmodule

module jeuswitchcore (
  input  DS1,
  input  DS2,
  input  DS3,
  input  DS4,
  input  DS5,
  input  DS6,
  input  DS7,
  input  DS8,
  input  Clock,
  input  ClockOrigin,
  input  Reset,
  output LED1,
  output LED2,
  output LED3,
  output LED4,
  output LED5,
  output LED6,
  output LED7,
  output LED8,
  output Point
);

  wire and_1_out, and_2_out, and_3_out, and_4_out, and_5_out, and_6_out, and_7_out, and_8_out,
       SwitchSwitch_1_switchstate, SwitchSwitch_2_switchstate, SwitchSwitch_3_switchstate,
       SwitchSwitch_4_switchstate, SwitchSwitch_5_switchstate, SwitchSwitch_6_switchstate,
       SwitchSwitch_7_switchstate, SwitchSwitch_8_switchstate;

  SwitchSwitch SwitchSwitch_1 (.Switch(DS1), .Clock(Clock), .Reset(Reset), .SwitchState(SwitchSwitch_1_switchstate));
  SwitchSwitch SwitchSwitch_2 (.Switch(DS2), .Clock(Clock), .Reset(Reset), .SwitchState(SwitchSwitch_2_switchstate));
  SwitchSwitch SwitchSwitch_3 (.Switch(DS3), .Clock(Clock), .Reset(Reset), .SwitchState(SwitchSwitch_3_switchstate));
  SwitchSwitch SwitchSwitch_4 (.Switch(DS4), .Clock(Clock), .Reset(Reset), .SwitchState(SwitchSwitch_4_switchstate));
  SwitchSwitch SwitchSwitch_5 (.Switch(DS5), .Clock(Clock), .Reset(Reset), .SwitchState(SwitchSwitch_5_switchstate));
  SwitchSwitch SwitchSwitch_6 (.Switch(DS6), .Clock(Clock), .Reset(Reset), .SwitchState(SwitchSwitch_6_switchstate));
  SwitchSwitch SwitchSwitch_7 (.Switch(DS7), .Clock(Clock), .Reset(Reset), .SwitchState(SwitchSwitch_7_switchstate));
  SwitchSwitch SwitchSwitch_8 (.Switch(DS8), .Clock(Clock), .Reset(Reset), .SwitchState(SwitchSwitch_8_switchstate));
  and and_1 (and_1_out, LED1, SwitchSwitch_1_switchstate);
  and and_2 (and_2_out, LED2, SwitchSwitch_2_switchstate);
  and and_3 (and_3_out, LED3, SwitchSwitch_3_switchstate);
  and and_4 (and_4_out, LED4, SwitchSwitch_4_switchstate);
  and and_5 (and_5_out, LED5, SwitchSwitch_5_switchstate);
  and and_6 (and_6_out, LED6, SwitchSwitch_6_switchstate);
  and and_7 (and_7_out, LED7, SwitchSwitch_7_switchstate);
  and and_8 (and_8_out, LED8, SwitchSwitch_8_switchstate);
  or or_1 (Point, and_1_out, and_2_out, and_3_out, and_4_out, and_5_out, and_6_out, and_7_out, and_8_out);
  LEDGen LEDGen_1 (
    .SwitchOK(Point), .Clock(ClockOrigin), .LED1(LED1), .LED2(LED2), .LED3(LED3), .LED4(LED4), .LED5(LED5),
    .LED6(LED6), .LED7(LED7), .LED8(LED8));
endmodule

module SwitchSwitch (
  input  Switch,
  input  Clock,
  input  Reset,
  output SwitchState
);

  wire d_ff_1_q, d_ff_2_q, not_1_out;

  D_Flip_Flop d_ff_1 (.D(1'b0), .clk(Clock), .Q(d_ff_1_q), .preset(Switch), .reset(Reset));  // open: Qn
  not not_1 (not_1_out, Switch);
  D_Flip_Flop d_ff_2 (.D(1'b0), .clk(Clock), .Q(d_ff_2_q), .preset(not_1_out), .reset(Reset));  // open: Qn
  Multiplexer #(.enable("false")) multiplexer_1 (.in0(d_ff_1_q), .in1(d_ff_2_q), .out(SwitchState), .sel(Switch));
endmodule

module LEDGen (
  input  SwitchOK,
  input  Clock,
  output LED1,
  output LED2,
  output LED3,
  output LED4,
  output LED5,
  output LED6,
  output LED7,
  output LED8
);

  wire [2:0] random_1_out;

  Random #(.width(3)) random_1 (.clr(1'b0), .next(SwitchOK), .clk(Clock), .out(random_1_out));
  Demultiplexer #(.select(3), .enable("false")) demultiplexer_1 (
    .out0(LED1), .out1(LED2), .out2(LED3), .out3(LED4), .out4(LED5), .out5(LED6), .out6(LED7), .out7(LED8),
    .in(1'b1), .sel(random_1_out));
endmodule

module save_score (
  input  [3:0] U_score_in,
  input  [3:0] D_score_in,
  input  Save_Mode,
  input  Reset,
  output [3:0] U_score_out,
  output [3:0] D_score_out
);

  wire d_ff_1_q;
  wire [3:0] compt_u_sec_s2_o, compt_u_sec_s_o;

  D_Flip_Flop d_ff_1 (.D(1'b0), .clk(1'b0), .Q(d_ff_1_q), .preset(Save_Mode), .reset(Reset));  // open: Qn
  compt_u_sec_m compt_u_sec_s (
    .Trigger(1'b1), .Clock(1'b0), .Reset(Reset), .U_sec_m_set(U_score_out), .SET_OK(1'b1), .O(compt_u_sec_s_o));  // open: Retenu
  compt_u_sec_m compt_u_sec_s2 (
    .Trigger(1'b1), .Clock(1'b0), .Reset(Reset), .U_sec_m_set(D_score_out), .SET_OK(1'b1),
    .O(compt_u_sec_s2_o));  // open: Retenu
  Multiplexer #(.width(4), .enable("false")) multiplexer_1 (
    .in0(U_score_in), .in1(compt_u_sec_s_o), .out(U_score_out), .sel(d_ff_1_q));
  Multiplexer #(.width(4), .enable("false")) multiplexer_2 (
    .in0(D_score_in), .in1(compt_u_sec_s2_o), .out(D_score_out), .sel(d_ff_1_q));
endmodule

module JEUMEMORY (
  input  ME,
  input  [7:0] Switch,
  input  Reset,
  input  Clock1HZ,
  input  Clock,
  output LED1,
  output LED2,
  output LED3,
  output LED4,
  output LED5,
  output LED6,
  output LED7,
  output LED8,
  output [3:0] TPS,
  output [3:0] U_Point,
  output [3:0] D_Point
);

  wire and_1_out, and_2_out, and_3_out, and_4_out, and_5_out, comparator_1_eq, comparator_1_gt,
       comparator_2_eq, comparator_3_gt, comparator_3_lt, comparator_4_eq, COMPPoint_retenu, d_ff_9_q,
       or_1_out, or_2_out, or_3_out, s_r_ff_1_q;
  wire [3:0] adder_1_out, adder_2_out, bit_extender_1_out, bit_extender_2_out, d_ff_7_q, d_ff_8_q;
  wire [7:0] random_1_out;

  Comparator comparator_1 (.a(Switch), .b({8{1'b0}}), .gt(comparator_1_gt), .eq(comparator_1_eq));  // open: lt
  and and_1 (and_1_out, comparator_1_gt, comparator_3_gt);
  or or_1 (or_1_out, and_1_out, comparator_2_eq, Reset, comparator_4_eq);
  and and_2 (and_2_out, ~comparator_3_lt, comparator_1_eq, ME);  // AND_Gate
  and and_3 (and_3_out, comparator_3_lt, ME);
  Random random_1 (.clr(1'b0), .next(and_4_out), .clk(Clock), .out(random_1_out));
  and and_4 (and_4_out, ME, or_1_out);
  assign bit_extender_1_out = {{3{1'b0}}, and_2_out};  // Bit_Extender bit_extender_1
  assign bit_extender_2_out = {{3{1'b0}}, and_3_out};  // Bit_Extender bit_extender_2
  Adder #(.width(4)) adder_1 (.a(d_ff_7_q), .b(bit_extender_1_out), .out(adder_1_out), .cin(1'b0));  // open: cout
  D_Flip_Flop d_ff_1 (
    .D(adder_1_out[3]), .clk(Clock1HZ), .Q(d_ff_7_q[3]), .preset(1'b0), .reset(or_1_out));  // open: Qn
  Adder #(.width(4)) adder_2 (.a(d_ff_8_q), .b(bit_extender_2_out), .out(adder_2_out), .cin(1'b0));  // open: cout
  D_Flip_Flop d_ff_2 (
    .D(adder_2_out[3]), .clk(Clock1HZ), .Q(d_ff_8_q[3]), .preset(1'b0), .reset(or_1_out));  // open: Qn
  D_Flip_Flop d_ff_3 (
    .D(adder_1_out[2]), .clk(Clock1HZ), .Q(d_ff_7_q[2]), .preset(1'b0), .reset(or_1_out));  // open: Qn
  D_Flip_Flop d_ff_4 (
    .D(adder_2_out[2]), .clk(Clock1HZ), .Q(d_ff_8_q[2]), .preset(1'b0), .reset(or_1_out));  // open: Qn
  Comparator comparator_2 (.a(Switch), .b(random_1_out), .eq(comparator_2_eq));  // open: gt, lt
  D_Flip_Flop d_ff_5 (
    .D(adder_1_out[1]), .clk(Clock1HZ), .Q(d_ff_7_q[1]), .preset(1'b0), .reset(or_1_out));  // open: Qn
  D_Flip_Flop d_ff_6 (
    .D(adder_2_out[1]), .clk(Clock1HZ), .Q(d_ff_8_q[1]), .preset(1'b0), .reset(or_1_out));  // open: Qn
  S_R_Flip_Flop s_r_ff_1 (
    .S(1'b0), .R(1'b0), .clk(1'b0), .Q(s_r_ff_1_q), .reset(or_2_out), .preset(comparator_2_eq));  // open: Qn
  or or_2 (or_2_out, Reset, d_ff_9_q);
  D_Flip_Flop d_ff_7 (
    .D(adder_1_out[0]), .clk(Clock1HZ), .Q(d_ff_7_q[0]), .preset(1'b0), .reset(or_1_out));  // open: Qn
  D_Flip_Flop d_ff_8 (
    .D(adder_2_out[0]), .clk(Clock1HZ), .Q(d_ff_8_q[0]), .preset(1'b0), .reset(or_1_out));  // open: Qn
  Comparator #(.width(4), .mode("unsigned")) comparator_3 (
    .a(4'b0100), .b(d_ff_7_q), .gt(comparator_3_gt), .lt(comparator_3_lt));  // open: eq
  Comparator #(.width(4), .mode("unsigned")) comparator_4 (
    .a(4'b1010), .b(d_ff_8_q), .eq(comparator_4_eq));  // open: gt, lt
  Multiplexer #(.width(8)) multiplexer_1 (
    .in0(random_1_out), .in1(Switch), .out({LED1, LED2, LED3, LED4, LED5, LED6, LED7, LED8}),
    .sel(comparator_3_lt), .en(ME));
  Multiplexer #(.width(4)) multiplexer_2 (.in0(d_ff_7_q), .in1(d_ff_8_q), .out(TPS), .sel(comparator_3_lt), .en(ME));
  and and_5 (and_5_out, ~and_4_out, s_r_ff_1_q);  // AND_Gate
  or or_3 (or_3_out, comparator_4_eq, Reset);
  D_Flip_Flop d_ff_9 (.D(and_5_out), .clk(Clock), .Q(d_ff_9_q), .preset(1'b0), .reset(Reset));  // open: Qn
  compt_u_sec_m COMPPoint (
    .Trigger(1'b1), .Clock(d_ff_9_q), .Reset(or_3_out), .U_sec_m_set(4'b0000), .SET_OK(1'b0),
    .Retenu(COMPPoint_retenu), .O(U_Point));
  compt_u_sec_m COMPPoint2 (
    .Trigger(1'b1), .Clock(COMPPoint_retenu), .Reset(or_3_out), .U_sec_m_set(4'b0000), .SET_OK(1'b0),
    .O(D_Point));  // open: Retenu
endmodule

module DECODEURCPTL (
  input  Reset,
  input  CHA,
  input  CHB,
  input  Clock,
  output CW,
  output CCW,
  output en_cnt
);

  wire AntiReb_7_s, AntiReb_8_s;

  AntiReb AntiReb_7 (.E(CHA), .Clock(Clock), .Reset(Reset), .S(AntiReb_7_s));
  AntiReb AntiReb_8 (.E(CHB), .Clock(Clock), .Reset(Reset), .S(AntiReb_8_s));
  DecodeurCoeur DecodeurCoeur2_3 (.CHA(AntiReb_7_s), .CHB(AntiReb_8_s), .CW(CW), .CCW(CCW));
  or or_1 (en_cnt, CW, CCW);
endmodule

module DecodeurCoeur (
  input  CHA,
  input  CHB,
  output CW,
  output CCW
);

  wire and_1_out, and_2_out, and_3_out, and_4_out, and_5_out, and_6_out, and_7_out, and_8_out, d_ff_1_q,
       d_ff_2_q, d_ff_3_q, d_ff_4_q, not_1_out, not_2_out, not_3_out, not_4_out, not_5_out, not_6_out,
       not_7_out, not_8_out;

  not not_1 (not_1_out, CHB);
  and and_1 (and_1_out, CHA, CHB);
  not not_2 (not_2_out, CHB);
  not not_3 (not_3_out, CHA);
  and and_2 (and_2_out, CHA, not_1_out);
  not not_4 (not_4_out, CHB);
  not not_5 (not_5_out, CHA);
  and and_3 (and_3_out, CHA, CHB);
  not not_6 (not_6_out, CHA);
  D_Flip_Flop d_ff_1 (.D(1'b0), .clk(1'b0), .Q(d_ff_1_q), .preset(and_1_out), .reset(not_4_out));  // open: Qn
  not not_7 (not_7_out, CHA);
  and and_4 (and_4_out, not_2_out, not_6_out);
  D_Flip_Flop d_ff_2 (.D(1'b0), .clk(1'b0), .Q(d_ff_2_q), .preset(not_3_out), .reset(CHB));  // open: Qn
  D_Flip_Flop d_ff_3 (.D(1'b0), .clk(1'b0), .Q(d_ff_3_q), .preset(and_3_out), .reset(not_7_out));  // open: Qn
  D_Flip_Flop d_ff_4 (.D(1'b0), .clk(1'b0), .Q(d_ff_4_q), .preset(and_4_out), .reset(CHA));  // open: Qn
  not not_8 (not_8_out, CHB);
  and and_5 (and_5_out, d_ff_2_q, and_2_out);
  and and_6 (and_6_out, d_ff_1_q, not_5_out);
  and and_7 (and_7_out, d_ff_4_q, CHB);
  or or_1 (CW, and_5_out, and_6_out);
  and and_8 (and_8_out, d_ff_3_q, not_8_out);
  or or_2 (CCW, and_8_out, and_7_out);
endmodule

module AntiReb (
  input  E,
  input  Clock,
  input  Reset,
  output S
);

  wire d_ff_1_q, d_ff_2_q, d_ff_3_q, d_ff_4_q;

  D_Flip_Flop d_ff_1 (.D(E), .clk(Clock), .Q(d_ff_1_q), .preset(1'b0), .reset(Reset));  // open: Qn
  D_Flip_Flop d_ff_2 (.D(d_ff_1_q), .clk(Clock), .Q(d_ff_2_q), .preset(1'b0), .reset(Reset));  // open: Qn
  D_Flip_Flop d_ff_3 (.D(d_ff_2_q), .clk(Clock), .Q(d_ff_3_q), .preset(1'b0), .reset(Reset));  // open: Qn
  D_Flip_Flop d_ff_4 (.D(d_ff_3_q), .clk(Clock), .Q(d_ff_4_q), .preset(1'b0), .reset(Reset));  // open: Qn
  and and_1 (S, d_ff_2_q, d_ff_3_q, d_ff_4_q);
endmodule

module COMPTEUR (
  input  Clock,
  input  Reset,
  input  Trigger,
  input  [3:0] D_h_set,
  input  [3:0] U_h_set,
  input  [3:0] D_min_set,
  input  [3:0] U_min_set,
  input  [3:0] D_sec_set,
  input  [3:0] U_sec_set,
  input  SET_OK,
  output [3:0] U_sec_Now,
  output [3:0] D_sec_Now,
  output [3:0] U_min_Now,
  output [3:0] D_min_Now,
  output [3:0] U_h_Now,
  output [3:0] D_h_Now
);

  wire comp_d_sec_m_11_retenu, comp_d_sec_m_21_retenu, compt_d_h_11_vingtaine, compt_u_h_12_anti_vingtaine,
       compt_u_h_12_retenu, compt_u_sec_m_11_retenu, compt_u_sec_m_22_retenu;

  compt_d_h compt_d_h_11 (
    .Trigger(Trigger), .Clock(compt_u_h_12_retenu), .Reset(Reset),
    .Anti_vingtaine(compt_u_h_12_anti_vingtaine), .D_h_set(D_h_set), .SET_OK(SET_OK), .O(D_h_Now),
    .Vingtaine(compt_d_h_11_vingtaine));
  compt_u_h compt_u_h_12 (
    .Vingtaine(compt_d_h_11_vingtaine), .Trigger(Trigger), .Clock(comp_d_sec_m_11_retenu), .Reset(Reset),
    .U_h_set(U_h_set), .SET_OK(SET_OK), .Retenu(compt_u_h_12_retenu), .O(U_h_Now),
    .Anti_Vingtaine(compt_u_h_12_anti_vingtaine));
  comp_d_sec_m comp_d_sec_m_11 (
    .Trigger(Trigger), .Clock(compt_u_sec_m_11_retenu), .Reset(Reset), .D_sec_m_set(D_min_set),
    .SET_OK(SET_OK), .Retenu(comp_d_sec_m_11_retenu), .O(D_min_Now));
  compt_u_sec_m compt_u_sec_m_11 (
    .Trigger(Trigger), .Clock(comp_d_sec_m_21_retenu), .Reset(Reset), .U_sec_m_set(U_min_set),
    .SET_OK(SET_OK), .Retenu(compt_u_sec_m_11_retenu), .O(U_min_Now));
  comp_d_sec_m comp_d_sec_m_21 (
    .Trigger(Trigger), .Clock(compt_u_sec_m_22_retenu), .Reset(Reset), .D_sec_m_set(D_sec_set),
    .SET_OK(SET_OK), .Retenu(comp_d_sec_m_21_retenu), .O(D_sec_Now));
  compt_u_sec_m compt_u_sec_m_22 (
    .Trigger(Trigger), .Clock(Clock), .Reset(Reset), .U_sec_m_set(U_sec_set), .SET_OK(SET_OK),
    .Retenu(compt_u_sec_m_22_retenu), .O(U_sec_Now));
endmodule

module compt_u_sec_m (
  input  Trigger,
  input  Clock,
  input  Reset,
  input  [3:0] U_sec_m_set,
  input  SET_OK,
  output Retenu,
  output [3:0] O
);

  wire comparator_1_gt, d_ff_3_q, nand_1_out;
  wire [3:0] adder_1_out, bit_extender_1_out, bit_extender_2_out, d_ff_5_q, multiplexer_1_out,
       multiplexer_2_out;

  assign bit_extender_1_out = {{3{1'b0}}, Trigger};  // Bit_Extender bit_extender_1
  Adder #(.width(4)) adder_1 (
    .a(multiplexer_2_out), .b(bit_extender_1_out), .out(adder_1_out), .cin(1'b0));  // open: cout
  D_Flip_Flop d_ff_1 (.D(adder_1_out[3]), .clk(Clock), .Q(d_ff_5_q[3]), .preset(1'b0), .reset(Reset));  // open: Qn
  D_Flip_Flop d_ff_2 (.D(adder_1_out[2]), .clk(Clock), .Q(d_ff_5_q[2]), .preset(1'b0), .reset(Reset));  // open: Qn
  D_Flip_Flop d_ff_3 (.D(1'b0), .clk(Clock), .Q(d_ff_3_q), .preset(SET_OK), .reset(Reset));  // open: Qn
  D_Flip_Flop d_ff_4 (.D(adder_1_out[1]), .clk(Clock), .Q(d_ff_5_q[1]), .preset(1'b0), .reset(Reset));  // open: Qn
  D_Flip_Flop d_ff_5 (.D(adder_1_out[0]), .clk(Clock), .Q(d_ff_5_q[0]), .preset(1'b0), .reset(Reset));  // open: Qn
  Multiplexer #(.width(4), .enable("false")) multiplexer_1 (
    .in0(d_ff_5_q), .in1(U_sec_m_set), .out(multiplexer_1_out), .sel(d_ff_3_q));
  Multiplexer #(.width(4), .enable("false")) multiplexer_2 (
    .in0(4'b0000), .in1(multiplexer_1_out), .out(multiplexer_2_out), .sel(comparator_1_gt));
  Comparator #(.width(4), .mode("unsigned")) comparator_1 (
    .a(4'b1010), .b(multiplexer_1_out), .gt(comparator_1_gt));  // open: eq, lt
  Comparator #(.width(4)) comparator_2 (.a(multiplexer_1_out), .b(4'b1010), .eq(Retenu));  // open: gt, lt
  Multiplexer #(.width(4), .enable("false")) multiplexer_3 (
    .in0(multiplexer_1_out), .in1(bit_extender_2_out), .out(O), .sel(Retenu));
  nand nand_1 (nand_1_out, Retenu, 1'b1);
  assign bit_extender_2_out = {{3{nand_1_out}}, nand_1_out};  // Bit_Extender bit_extender_2
endmodule

module comp_d_sec_m (
  input  Trigger,
  input  Clock,
  input  Reset,
  input  [3:0] D_sec_m_set,
  input  SET_OK,
  output Retenu,
  output [3:0] O
);

  wire comparator_1_gt, d_ff_3_q, nand_1_out;
  wire [3:0] adder_1_out, bit_extender_1_out, bit_extender_2_out, d_ff_5_q, multiplexer_1_out,
       multiplexer_2_out;

  assign bit_extender_1_out = {{3{1'b0}}, Trigger};  // Bit_Extender bit_extender_1
  Adder #(.width(4)) adder_1 (
    .a(multiplexer_2_out), .b(bit_extender_1_out), .out(adder_1_out), .cin(1'b0));  // open: cout
  D_Flip_Flop d_ff_1 (.D(adder_1_out[3]), .clk(Clock), .Q(d_ff_5_q[3]), .preset(1'b0), .reset(Reset));  // open: Qn
  D_Flip_Flop d_ff_2 (.D(adder_1_out[2]), .clk(Clock), .Q(d_ff_5_q[2]), .preset(1'b0), .reset(Reset));  // open: Qn
  D_Flip_Flop d_ff_3 (.D(1'b0), .clk(Clock), .Q(d_ff_3_q), .preset(SET_OK), .reset(Reset));  // open: Qn
  D_Flip_Flop d_ff_4 (.D(adder_1_out[1]), .clk(Clock), .Q(d_ff_5_q[1]), .preset(1'b0), .reset(Reset));  // open: Qn
  D_Flip_Flop d_ff_5 (.D(adder_1_out[0]), .clk(Clock), .Q(d_ff_5_q[0]), .preset(1'b0), .reset(Reset));  // open: Qn
  Multiplexer #(.width(4), .enable("false")) multiplexer_1 (
    .in0(d_ff_5_q), .in1(D_sec_m_set), .out(multiplexer_1_out), .sel(d_ff_3_q));
  Multiplexer #(.width(4), .enable("false")) multiplexer_2 (
    .in0(4'b0000), .in1(multiplexer_1_out), .out(multiplexer_2_out), .sel(comparator_1_gt));
  Comparator #(.width(4), .mode("unsigned")) comparator_1 (
    .a(4'b0110), .b(multiplexer_1_out), .gt(comparator_1_gt));  // open: eq, lt
  Comparator #(.width(4)) comparator_2 (.a(multiplexer_1_out), .b(4'b0110), .eq(Retenu));  // open: gt, lt
  nand nand_1 (nand_1_out, Retenu, 1'b1);
  Multiplexer #(.width(4), .enable("false")) multiplexer_3 (
    .in0(multiplexer_1_out), .in1(bit_extender_2_out), .out(O), .sel(Retenu));
  assign bit_extender_2_out = {{3{nand_1_out}}, nand_1_out};  // Bit_Extender bit_extender_2
endmodule

module compt_u_h (
  input  Vingtaine,
  input  Trigger,
  input  Clock,
  input  Reset,
  input  [3:0] U_h_set,
  input  SET_OK,
  output Retenu,
  output [3:0] O,
  output Anti_Vingtaine
);

  wire comparator_1_eq, comparator_2_gt, comparator_3_gt, comparator_4_eq, d_ff_1_q, d_ff_6_q,
       multiplexer_4_out, nand_1_out, nand_2_out;
  wire [3:0] adder_1_out, bit_extender_1_out, bit_extender_2_out, bit_extender_3_out, d_ff_5_q,
       multiplexer_1_out, multiplexer_2_out, multiplexer_3_out, multiplexer_5_out;

  D_Flip_Flop d_ff_1 (.D(Vingtaine), .clk(Clock), .Q(d_ff_1_q), .preset(1'b0), .reset(1'b0));  // open: Qn
  assign bit_extender_1_out = {{3{1'b0}}, Trigger};  // Bit_Extender bit_extender_1
  Adder #(.width(4)) adder_1 (
    .a(multiplexer_3_out), .b(bit_extender_1_out), .out(adder_1_out), .cin(1'b0));  // open: cout
  Comparator #(.width(4)) comparator_1 (.a(multiplexer_2_out), .b(4'b0100), .eq(comparator_1_eq));  // open: gt, lt
  D_Flip_Flop d_ff_2 (.D(adder_1_out[3]), .clk(Clock), .Q(d_ff_5_q[3]), .preset(1'b0), .reset(Reset));  // open: Qn
  Multiplexer #(.width(4), .enable("false")) multiplexer_1 (
    .in0(multiplexer_2_out), .in1(bit_extender_2_out), .out(multiplexer_1_out), .sel(comparator_1_eq));
  D_Flip_Flop d_ff_3 (.D(adder_1_out[2]), .clk(Clock), .Q(d_ff_5_q[2]), .preset(1'b0), .reset(Reset));  // open: Qn
  nand nand_1 (nand_1_out, comparator_1_eq, 1'b1);
  D_Flip_Flop d_ff_4 (.D(adder_1_out[1]), .clk(Clock), .Q(d_ff_5_q[1]), .preset(1'b0), .reset(Reset));  // open: Qn
  assign bit_extender_2_out = {{3{nand_1_out}}, nand_1_out};  // Bit_Extender bit_extender_2
  D_Flip_Flop d_ff_5 (.D(adder_1_out[0]), .clk(Clock), .Q(d_ff_5_q[0]), .preset(1'b0), .reset(Reset));  // open: Qn
  D_Flip_Flop d_ff_6 (.D(1'b0), .clk(Clock), .Q(d_ff_6_q), .preset(SET_OK), .reset(Reset));  // open: Qn
  Multiplexer #(.width(4), .enable("false")) multiplexer_2 (
    .in0(d_ff_5_q), .in1(U_h_set), .out(multiplexer_2_out), .sel(d_ff_6_q));
  Comparator #(.width(4), .mode("unsigned")) comparator_2 (
    .a(4'b1010), .b(multiplexer_2_out), .gt(comparator_2_gt));  // open: eq, lt
  Comparator #(.width(4), .mode("unsigned")) comparator_3 (
    .a(4'b0100), .b(multiplexer_2_out), .gt(comparator_3_gt));  // open: eq, lt
  Multiplexer #(.width(4), .enable("false")) multiplexer_3 (
    .in0(4'b0000), .in1(multiplexer_2_out), .out(multiplexer_3_out), .sel(multiplexer_4_out));
  Multiplexer #(.enable("false")) multiplexer_4 (
    .in0(comparator_2_gt), .in1(comparator_3_gt), .out(multiplexer_4_out), .sel(d_ff_1_q));
  Comparator #(.width(4)) comparator_4 (.a(multiplexer_2_out), .b(4'b1010), .eq(comparator_4_eq));  // open: gt, lt
  Multiplexer #(.width(4), .enable("false")) multiplexer_5 (
    .in0(multiplexer_2_out), .in1(bit_extender_3_out), .out(multiplexer_5_out), .sel(comparator_4_eq));
  Multiplexer #(.enable("false")) multiplexer_6 (
    .in0(comparator_4_eq), .in1(comparator_1_eq), .out(Retenu), .sel(d_ff_1_q));
  nand nand_2 (nand_2_out, comparator_4_eq, 1'b1);
  Multiplexer #(.width(4), .enable("false")) multiplexer_7 (
    .in0(multiplexer_5_out), .in1(multiplexer_1_out), .out(O), .sel(d_ff_1_q));
  assign bit_extender_3_out = {{3{nand_2_out}}, nand_2_out};  // Bit_Extender bit_extender_3
  Comparator #(.width(4)) comparator_5 (.a(4'b0011), .b(O), .lt(Anti_Vingtaine));  // open: gt, eq
endmodule

module compt_d_h (
  input  Trigger,
  input  Clock,
  input  Reset,
  input  Anti_vingtaine,
  input  [3:0] D_h_set,
  input  SET_OK,
  output [3:0] O,
  output Vingtaine
);

  wire comparator_1_gt, comparator_2_eq, d_ff_4_q, nand_1_out;
  wire [3:0] adder_1_out, bit_extender_1_out, bit_extender_2_out, d_ff_5_q, multiplexer_1_out,
       multiplexer_2_out, multiplexer_3_out, multiplexer_4_out;

  assign bit_extender_1_out = {{3{1'b0}}, Trigger};  // Bit_Extender bit_extender_1
  Adder #(.width(4)) adder_1 (
    .a(multiplexer_4_out), .b(bit_extender_1_out), .out(adder_1_out), .cin(1'b0));  // open: cout
  D_Flip_Flop d_ff_1 (.D(adder_1_out[3]), .clk(Clock), .Q(d_ff_5_q[3]), .preset(1'b0), .reset(Reset));  // open: Qn
  D_Flip_Flop d_ff_2 (.D(adder_1_out[2]), .clk(Clock), .Q(d_ff_5_q[2]), .preset(1'b0), .reset(Reset));  // open: Qn
  D_Flip_Flop d_ff_3 (.D(adder_1_out[1]), .clk(Clock), .Q(d_ff_5_q[1]), .preset(1'b0), .reset(Reset));  // open: Qn
  D_Flip_Flop d_ff_4 (.D(1'b0), .clk(Clock), .Q(d_ff_4_q), .preset(SET_OK), .reset(Reset));  // open: Qn
  D_Flip_Flop d_ff_5 (.D(adder_1_out[0]), .clk(Clock), .Q(d_ff_5_q[0]), .preset(1'b0), .reset(Reset));  // open: Qn
  Multiplexer #(.width(4), .enable("false")) multiplexer_1 (
    .in0(d_ff_5_q), .in1(D_h_set), .out(multiplexer_1_out), .sel(d_ff_4_q));
  Multiplexer #(.width(4), .enable("false")) multiplexer_2 (
    .in0(4'b0011), .in1(4'b0010), .out(multiplexer_2_out), .sel(Anti_vingtaine));
  Comparator #(.width(4), .mode("unsigned")) comparator_1 (
    .a(multiplexer_2_out), .b(multiplexer_1_out), .gt(comparator_1_gt));  // open: eq, lt
  Multiplexer #(.width(4), .enable("false")) multiplexer_3 (
    .in0(4'b0011), .in1(4'b0010), .out(multiplexer_3_out), .sel(Anti_vingtaine));
  Multiplexer #(.width(4), .enable("false")) multiplexer_4 (
    .in0(4'b0000), .in1(multiplexer_1_out), .out(multiplexer_4_out), .sel(comparator_1_gt));
  Comparator #(.width(4)) comparator_2 (
    .a(multiplexer_1_out), .b(multiplexer_3_out), .eq(comparator_2_eq));  // open: gt, lt
  Multiplexer #(.width(4), .enable("false")) multiplexer_5 (
    .in0(multiplexer_1_out), .in1(bit_extender_2_out), .out(O), .sel(comparator_2_eq));
  nand nand_1 (nand_1_out, comparator_2_eq, 1'b1);
  assign bit_extender_2_out = {{3{nand_1_out}}, nand_1_out};  // Bit_Extender bit_extender_2
  Comparator #(.width(4)) comparator_3 (.a(O), .b(4'b0010), .eq(Vingtaine));  // open: gt, lt
endmodule

module DECOMPTEUR (
  input  Clock,
  input  Reset,
  input  Trigger,
  input  [3:0] D_h_set,
  input  [3:0] U_h_set,
  input  [3:0] D_min_set,
  input  [3:0] U_min_set,
  input  [3:0] D_sec_set,
  input  [3:0] U_sec_set,
  input  SET_OK,
  output [3:0] U_sec_Now,
  output [3:0] D_sec_Now,
  output [3:0] U_min_Now,
  output [3:0] D_min_Now,
  output [3:0] U_h_Now,
  output [3:0] D_h_Now
);

  wire decompt_d_h_1_vingtaine, decompt_d_sec_m_1_retenu, decompt_d_sec_m_2_retenu, decompt_u_h_1_retenu,
       decompt_u_sec_m_1_retenu, decompt_u_sec_m_2_retenu;

  decompt_d_h decompt_d_h_1 (
    .Trigger(Trigger), .Clock(decompt_u_h_1_retenu), .Reset(Reset), .D_h_set(D_h_set), .SET_OK(SET_OK),
    .O(D_h_Now), .Vingtaine(decompt_d_h_1_vingtaine));  // open: Retenu
  decompt_u_h decompt_u_h_1 (
    .Vingtaine(decompt_d_h_1_vingtaine), .Trigger(Trigger), .Clock(decompt_d_sec_m_2_retenu), .Reset(Reset),
    .U_h_set(U_h_set), .SET_OK(SET_OK), .Retenu(decompt_u_h_1_retenu), .O(U_h_Now));
  decompt_d_sec_m decompt_d_sec_m_2 (
    .Trigger(Trigger), .Clock(decompt_u_sec_m_1_retenu), .Reset(Reset), .D_sec_min_set(D_min_set),
    .SET_OK(SET_OK), .O(D_min_Now), .Retenu(decompt_d_sec_m_2_retenu));
  decompt_u_sec_m decompt_u_sec_m_1 (
    .Trigger(Trigger), .Clock(decompt_d_sec_m_1_retenu), .Reset(Reset), .U_sec_m_set(U_min_set),
    .SET_OK(SET_OK), .Retenu(decompt_u_sec_m_1_retenu), .O(U_min_Now));
  decompt_d_sec_m decompt_d_sec_m_1 (
    .Trigger(Trigger), .Clock(decompt_u_sec_m_2_retenu), .Reset(Reset), .D_sec_min_set(D_sec_set),
    .SET_OK(SET_OK), .O(D_sec_Now), .Retenu(decompt_d_sec_m_1_retenu));
  decompt_u_sec_m decompt_u_sec_m_2 (
    .Trigger(Trigger), .Clock(Clock), .Reset(Reset), .U_sec_m_set(U_sec_set), .SET_OK(SET_OK),
    .Retenu(decompt_u_sec_m_2_retenu), .O(U_sec_Now));
endmodule

module decompt_u_sec_m (
  input  Trigger,
  input  Clock,
  input  Reset,
  input  [3:0] U_sec_m_set,
  input  SET_OK,
  output Retenu,
  output [3:0] O
);

  wire and_1_out, and_2_out, comparator_1_eq, comparator_1_lt, d_ff_5_q;
  wire [3:0] bit_extender_1_out, d_ff_4_q, multiplexer_2_out, subtractor_1_out;

  and and_1 (and_1_out, Trigger, Clock);
  assign bit_extender_1_out = {{3{1'b0}}, Trigger};  // Bit_Extender bit_extender_1
  Subtractor #(.width(4)) subtractor_1 (
    .a(multiplexer_2_out), .b(bit_extender_1_out), .out(subtractor_1_out), .bin(1'b0));  // open: bout
  D_Flip_Flop d_ff_1 (
    .D(subtractor_1_out[3]), .clk(and_1_out), .Q(d_ff_4_q[3]), .preset(1'b0), .reset(Reset));  // open: Qn
  D_Flip_Flop d_ff_2 (
    .D(subtractor_1_out[2]), .clk(and_1_out), .Q(d_ff_4_q[2]), .preset(1'b0), .reset(Reset));  // open: Qn
  D_Flip_Flop d_ff_3 (
    .D(subtractor_1_out[1]), .clk(and_1_out), .Q(d_ff_4_q[1]), .preset(1'b0), .reset(Reset));  // open: Qn
  D_Flip_Flop d_ff_4 (
    .D(subtractor_1_out[0]), .clk(and_1_out), .Q(d_ff_4_q[0]), .preset(1'b0), .reset(Reset));  // open: Qn
  D_Flip_Flop d_ff_5 (.D(1'b0), .clk(and_1_out), .Q(d_ff_5_q), .preset(SET_OK), .reset(Reset));  // open: Qn
  Comparator #(.width(4), .mode("unsigned")) comparator_1 (
    .a(4'b0000), .b(O), .eq(comparator_1_eq), .lt(comparator_1_lt));  // open: gt
  Multiplexer #(.width(4), .enable("false")) multiplexer_1 (.in0(d_ff_4_q), .in1(U_sec_m_set), .out(O), .sel(d_ff_5_q));
  Multiplexer #(.width(4), .enable("false")) multiplexer_2 (
    .in0(4'b1010), .in1(O), .out(multiplexer_2_out), .sel(comparator_1_lt));
  D_Flip_Flop d_ff_6 (.D(and_2_out), .clk(and_1_out), .Q(Retenu), .preset(1'b0), .reset(Reset));  // open: Qn
  and and_2 (and_2_out, comparator_1_eq, ~SET_OK);  // AND_Gate
endmodule

module decompt_d_sec_m (
  input  Trigger,
  input  Clock,
  input  Reset,
  input  [3:0] D_sec_min_set,
  input  SET_OK,
  output [3:0] O,
  output Retenu
);

  wire and_1_out, comparator_1_eq, comparator_1_lt, d_ff_5_q;
  wire [3:0] bit_extender_1_out, d_ff_4_q, multiplexer_2_out, subtractor_1_out;

  and and_1 (and_1_out, Trigger, Clock);
  assign bit_extender_1_out = {{3{1'b0}}, Trigger};  // Bit_Extender bit_extender_1
  Subtractor #(.width(4)) subtractor_1 (
    .a(multiplexer_2_out), .b(bit_extender_1_out), .out(subtractor_1_out), .bin(1'b0));  // open: bout
  D_Flip_Flop d_ff_1 (
    .D(subtractor_1_out[3]), .clk(and_1_out), .Q(d_ff_4_q[3]), .preset(1'b0), .reset(Reset));  // open: Qn
  D_Flip_Flop d_ff_2 (
    .D(subtractor_1_out[2]), .clk(and_1_out), .Q(d_ff_4_q[2]), .preset(1'b0), .reset(Reset));  // open: Qn
  D_Flip_Flop d_ff_3 (
    .D(subtractor_1_out[1]), .clk(and_1_out), .Q(d_ff_4_q[1]), .preset(1'b0), .reset(Reset));  // open: Qn
  D_Flip_Flop d_ff_4 (
    .D(subtractor_1_out[0]), .clk(and_1_out), .Q(d_ff_4_q[0]), .preset(1'b0), .reset(Reset));  // open: Qn
  D_Flip_Flop d_ff_5 (.D(1'b0), .clk(and_1_out), .Q(d_ff_5_q), .preset(SET_OK), .reset(Reset));  // open: Qn
  Comparator #(.width(4), .mode("unsigned")) comparator_1 (
    .a(4'b0000), .b(O), .eq(comparator_1_eq), .lt(comparator_1_lt));  // open: gt
  Multiplexer #(.width(4), .enable("false")) multiplexer_1 (
    .in0(d_ff_4_q), .in1(D_sec_min_set), .out(O), .sel(d_ff_5_q));
  Multiplexer #(.width(4), .enable("false")) multiplexer_2 (
    .in0(4'b0110), .in1(O), .out(multiplexer_2_out), .sel(comparator_1_lt));
  D_Flip_Flop d_ff_6 (.D(comparator_1_eq), .clk(and_1_out), .Q(Retenu), .preset(1'b0), .reset(Reset));  // open: Qn
endmodule

module decompt_u_h (
  input  Vingtaine,
  input  Trigger,
  input  Clock,
  input  Reset,
  input  [3:0] U_h_set,
  input  SET_OK,
  output Retenu,
  output [3:0] O
);

  wire and_1_out, comparator_1_eq, comparator_1_lt, d_ff_5_q;
  wire [3:0] bit_extender_1_out, d_ff_4_q, multiplexer_1_out, multiplexer_3_out, subtractor_1_out;

  assign bit_extender_1_out = {{3{1'b0}}, Trigger};  // Bit_Extender bit_extender_1
  and and_1 (and_1_out, Trigger, Clock);
  Subtractor #(.width(4)) subtractor_1 (
    .a(multiplexer_3_out), .b(bit_extender_1_out), .out(subtractor_1_out), .bin(1'b0));  // open: bout
  D_Flip_Flop d_ff_1 (
    .D(subtractor_1_out[3]), .clk(and_1_out), .Q(d_ff_4_q[3]), .preset(1'b0), .reset(Reset));  // open: Qn
  D_Flip_Flop d_ff_2 (
    .D(subtractor_1_out[2]), .clk(and_1_out), .Q(d_ff_4_q[2]), .preset(1'b0), .reset(Reset));  // open: Qn
  D_Flip_Flop d_ff_3 (
    .D(subtractor_1_out[1]), .clk(and_1_out), .Q(d_ff_4_q[1]), .preset(1'b0), .reset(Reset));  // open: Qn
  D_Flip_Flop d_ff_4 (
    .D(subtractor_1_out[0]), .clk(and_1_out), .Q(d_ff_4_q[0]), .preset(1'b0), .reset(Reset));  // open: Qn
  D_Flip_Flop d_ff_5 (.D(1'b0), .clk(and_1_out), .Q(d_ff_5_q), .preset(SET_OK), .reset(Reset));  // open: Qn
  Multiplexer #(.width(4), .enable("false")) multiplexer_1 (
    .in0(4'b1010), .in1(4'b0100), .out(multiplexer_1_out), .sel(Vingtaine));
  Comparator #(.width(4), .mode("unsigned")) comparator_1 (
    .a(4'b0000), .b(O), .eq(comparator_1_eq), .lt(comparator_1_lt));  // open: gt
  Multiplexer #(.width(4), .enable("false")) multiplexer_2 (.in0(d_ff_4_q), .in1(U_h_set), .out(O), .sel(d_ff_5_q));
  Multiplexer #(.width(4), .enable("false")) multiplexer_3 (
    .in0(multiplexer_1_out), .in1(O), .out(multiplexer_3_out), .sel(comparator_1_lt));
  D_Flip_Flop d_ff_6 (.D(comparator_1_eq), .clk(and_1_out), .Q(Retenu), .preset(1'b0), .reset(Reset));  // open: Qn
endmodule

module decompt_d_h (
  input  Trigger,
  input  Clock,
  input  Reset,
  input  [3:0] D_h_set,
  input  SET_OK,
  output [3:0] O,
  output Retenu,
  output Vingtaine
);

  wire and_1_out, comparator_1_lt, d_ff_5_q;
  wire [3:0] bit_extender_1_out, d_ff_4_q, multiplexer_2_out, subtractor_1_out;

  assign bit_extender_1_out = {{3{1'b0}}, Trigger};  // Bit_Extender bit_extender_1
  and and_1 (and_1_out, Trigger, Clock);
  Subtractor #(.width(4)) subtractor_1 (
    .a(multiplexer_2_out), .b(bit_extender_1_out), .out(subtractor_1_out), .bin(1'b0));  // open: bout
  D_Flip_Flop d_ff_1 (
    .D(subtractor_1_out[3]), .clk(and_1_out), .Q(d_ff_4_q[3]), .preset(1'b0), .reset(Reset));  // open: Qn
  D_Flip_Flop d_ff_2 (
    .D(subtractor_1_out[2]), .clk(and_1_out), .Q(d_ff_4_q[2]), .preset(1'b0), .reset(Reset));  // open: Qn
  D_Flip_Flop d_ff_3 (
    .D(subtractor_1_out[1]), .clk(and_1_out), .Q(d_ff_4_q[1]), .preset(1'b0), .reset(Reset));  // open: Qn
  D_Flip_Flop d_ff_4 (
    .D(subtractor_1_out[0]), .clk(and_1_out), .Q(d_ff_4_q[0]), .preset(1'b0), .reset(Reset));  // open: Qn
  Multiplexer #(.width(4), .enable("false")) multiplexer_1 (.in0(d_ff_4_q), .in1(D_h_set), .out(O), .sel(d_ff_5_q));
  D_Flip_Flop d_ff_5 (.D(1'b0), .clk(and_1_out), .Q(d_ff_5_q), .preset(SET_OK), .reset(Reset));  // open: Qn
  Comparator #(.width(4), .mode("unsigned")) comparator_1 (
    .a(4'b0000), .b(O), .eq(Retenu), .lt(comparator_1_lt));  // open: gt
  Multiplexer #(.width(4), .enable("false")) multiplexer_2 (
    .in0(4'b0011), .in1(O), .out(multiplexer_2_out), .sel(comparator_1_lt));
  Comparator #(.width(4)) comparator_2 (.a(O), .b(4'b0000), .eq(Vingtaine));  // open: gt, lt
endmodule

module mode (
  input  MODE_BTN,
  input  Clock,
  input  Reset,
  output [3:0] Mode
);

  wire comparator_1_gt;
  wire [3:0] adder_1_out, bit_extender_1_out, multiplexer_1_out;

  assign bit_extender_1_out = {{3{1'b0}}, MODE_BTN};  // Bit_Extender bit_extender_1
  Adder #(.width(4)) adder_1 (
    .a(multiplexer_1_out), .b(bit_extender_1_out), .out(adder_1_out), .cin(1'b0));  // open: cout
  D_Flip_Flop d_ff_1 (.D(adder_1_out[3]), .clk(Clock), .Q(Mode[3]), .preset(1'b0), .reset(Reset));  // open: Qn
  D_Flip_Flop d_ff_2 (.D(adder_1_out[2]), .clk(Clock), .Q(Mode[2]), .preset(1'b0), .reset(Reset));  // open: Qn
  D_Flip_Flop d_ff_3 (.D(adder_1_out[1]), .clk(Clock), .Q(Mode[1]), .preset(1'b0), .reset(Reset));  // open: Qn
  D_Flip_Flop d_ff_4 (.D(adder_1_out[0]), .clk(Clock), .Q(Mode[0]), .preset(1'b0), .reset(Reset));  // open: Qn
  Multiplexer #(.width(4), .enable("false")) multiplexer_1 (
    .in0(4'b0000), .in1(Mode), .out(multiplexer_1_out), .sel(comparator_1_gt));
  Comparator #(.width(4), .mode("unsigned")) comparator_1 (
    .a(4'b0110), .b(Mode), .gt(comparator_1_gt));  // open: eq, lt
endmodule

module ButtonDeb (
  input  E,
  input  Clock,
  input  Reset,
  output S
);

  wire d_ff_1_q, d_ff_2_qn;

  D_Flip_Flop d_ff_1 (.D(E), .clk(Clock), .Q(d_ff_1_q), .preset(1'b0), .reset(Reset));  // open: Qn
  D_Flip_Flop d_ff_2 (.D(d_ff_1_q), .clk(Clock), .Qn(d_ff_2_qn), .preset(1'b0), .reset(Reset));  // open: Q
  and and_1 (S, d_ff_1_q, d_ff_2_qn);
endmodule

module Buzzerie (
  input  Reset,
  input  Clock,
  output Buzzer
);

  wire comparator_1_gt, comparator_2_lt, comparator_3_gt, comparator_4_lt, comparator_5_gt, comparator_6_lt,
       comparator_7_gt, comparator_8_lt, counter_1_carry, counter_2_carry, counter_4_carry, counter_5_carry;
  wire [3:0] and_1_out;
  wire [9:0] counter_3_q;

  Counter #(.width(2), .max('h2)) counter_1 (
    .clr(Reset), .load(1'b0), .up(1'b1), .count(1'b1), .clk(Clock), .D(2'b00), .carry(counter_1_carry));  // open: Q
  Counter #(.width(1), .max('h1)) counter_2 (
    .clr(Reset), .load(1'b0), .up(1'b1), .count(1'b1), .clk(Clock), .D(1'b0), .carry(counter_2_carry));  // open: Q
  Counter #(.width(10), .max('h3ff)) counter_3 (
    .clr(Reset), .load(1'b0), .up(1'b1), .count(1'b1), .clk(Clock), .D({10{1'b0}}), .Q(counter_3_q));  // open: carry
  Counter #(.width(3), .max('h7)) counter_4 (
    .clr(Reset), .load(1'b0), .up(1'b1), .count(1'b1), .clk(Clock), .D(3'b000), .carry(counter_4_carry));  // open: Q
  Counter #(.width(2), .max('h3)) counter_5 (
    .clr(Reset), .load(1'b0), .up(1'b1), .count(1'b1), .clk(Clock), .D(2'b00), .carry(counter_5_carry));  // open: Q
  Comparator #(.width(10)) comparator_1 (.a(counter_3_q), .b(10'hcc), .gt(comparator_1_gt));  // open: eq, lt
  and and_1 (and_1_out[0], comparator_1_gt, comparator_2_lt);
  Comparator #(.width(10)) comparator_2 (.a(counter_3_q), .b(10'h198), .lt(comparator_2_lt));  // open: gt, eq
  Comparator #(.width(10)) comparator_3 (.a(counter_3_q), .b(10'h198), .gt(comparator_3_gt));  // open: eq, lt
  and and_2 (and_1_out[1], comparator_3_gt, comparator_4_lt);
  Comparator #(.width(10)) comparator_4 (.a(counter_3_q), .b(10'h264), .lt(comparator_4_lt));  // open: gt, eq
  Comparator #(.width(10)) comparator_5 (.a(counter_3_q), .b(10'h264), .gt(comparator_5_gt));  // open: eq, lt
  and and_3 (and_1_out[2], comparator_5_gt, comparator_6_lt);
  Comparator #(.width(10)) comparator_6 (.a(counter_3_q), .b(10'h330), .lt(comparator_6_lt));  // open: gt, eq
  Comparator #(.width(10)) comparator_7 (.a(counter_3_q), .b(10'h330), .gt(comparator_7_gt));  // open: eq, lt
  and and_4 (and_1_out[3], comparator_7_gt, comparator_8_lt);
  Comparator #(.width(10)) comparator_8 (.a(counter_3_q), .b(10'h3fc), .lt(comparator_8_lt));  // open: gt, eq
  Multiplexer #(.select(4), .enable("false")) multiplexer_1 (
    .in0(Clock), .in1(counter_2_carry), .in2(counter_1_carry), .in3(1'b0), .in4(counter_5_carry), .in5(1'b0),
    .in6(1'b0), .in7(1'b0), .in8(counter_4_carry), .in9(1'b0), .in10(1'b0), .in11(1'b0), .in12(1'b0),
    .in13(1'b0), .in14(1'b0), .in15(1'b0), .out(Buzzer), .sel(and_1_out));
endmodule

module affich (
  input  a0,
  input  b0,
  input  c0,
  input  d0,
  output a,
  output b,
  output c,
  output d,
  output e,
  output f,
  output g
);

  wire and_1_out, and_2_out, and_3_out, and_4_out, and_5_out, and_6_out, and_7_out, and_8_out, and_9_out,
       and_10_out, and_11_out, and_12_out, and_13_out, and_14_out, and_15_out, and_16_out, and_17_out,
       and_18_out, and_19_out, and_20_out, and_21_out, and_22_out, and_23_out, and_24_out, and_25_out,
       not_1_out, not_2_out, not_3_out, not_4_out, not_5_out, not_6_out, not_7_out, not_8_out, not_9_out,
       not_10_out, not_11_out, not_12_out, not_13_out, not_14_out, not_15_out, not_16_out, not_17_out,
       not_18_out, not_19_out, not_20_out, not_21_out, not_22_out, not_23_out, not_24_out, not_25_out,
       not_26_out, not_27_out, not_28_out, not_29_out, not_30_out, not_31_out, not_32_out;

  not not_1 (not_1_out, b0);
  and and_1 (and_1_out, not_1_out, not_2_out);
  not not_2 (not_2_out, d0);
  not not_3 (not_3_out, a0);
  and and_2 (and_2_out, not_3_out, c0);
  not not_4 (not_4_out, a0);
  and and_3 (and_3_out, not_4_out, b0, d0);
  and and_4 (and_4_out, a0, not_5_out);
  not not_5 (not_5_out, b0);
  and and_5 (and_5_out, a0, not_6_out);
  not not_6 (not_6_out, c0);
  and and_6 (and_6_out, a0, not_7_out);
  not not_7 (not_7_out, d0);
  not not_8 (not_8_out, b0);
  not not_9 (not_9_out, c0);
  and and_7 (and_7_out, not_9_out, not_10_out);
  not not_10 (not_10_out, d0);
  not not_11 (not_11_out, a0);
  and and_8 (and_8_out, not_11_out, c0, d0);
  not not_12 (not_12_out, c0);
  not not_13 (not_13_out, b0);
  and and_9 (and_9_out, not_13_out, d0);
  not not_14 (not_14_out, a0);
  and and_10 (and_10_out, not_14_out, b0);
  and and_11 (and_11_out, b0, not_15_out);
  not not_15 (not_15_out, d0);
  not not_16 (not_16_out, b0);
  and and_12 (and_12_out, not_16_out, not_17_out);
  not not_17 (not_17_out, d0);
  not not_18 (not_18_out, b0);
  and and_13 (and_13_out, not_18_out, c0);
  and and_14 (and_14_out, c0, not_19_out);
  not not_19 (not_19_out, d0);
  not not_20 (not_20_out, c0);
  and and_15 (and_15_out, b0, not_20_out, d0);
  not not_21 (not_21_out, b0);
  and and_16 (and_16_out, not_21_out, not_22_out);
  not not_22 (not_22_out, d0);
  and and_17 (and_17_out, c0, not_23_out);
  not not_23 (not_23_out, d0);
  not not_24 (not_24_out, c0);
  and and_18 (and_18_out, not_24_out, not_25_out);
  not not_25 (not_25_out, d0);
  and and_19 (and_19_out, b0, not_26_out);
  not not_26 (not_26_out, c0);
  and and_20 (and_20_out, b0, not_27_out);
  not not_27 (not_27_out, d0);
  and and_21 (and_21_out, a0, not_28_out);
  not not_28 (not_28_out, b0);
  not not_29 (not_29_out, b0);
  and and_22 (and_22_out, not_29_out, c0);
  and and_23 (and_23_out, b0, not_30_out);
  not not_30 (not_30_out, c0);
  and and_24 (and_24_out, b0, not_31_out);
  not not_31 (not_31_out, d0);
  and and_25 (and_25_out, a0, not_32_out);
  not not_32 (not_32_out, b0);
  or or_1 (b, not_8_out, and_7_out, and_8_out);
  or or_2 (c, not_12_out, and_9_out, and_10_out, and_11_out);
  or or_3 (d, and_12_out, and_13_out, and_14_out, and_15_out);
  or or_4 (e, and_16_out, and_17_out);
  or or_5 (f, and_18_out, and_19_out, and_20_out, and_21_out);
  or or_6 (g, and_22_out, and_23_out, and_24_out, and_25_out);
  or or_7 (a, and_1_out, and_2_out, and_3_out, and_4_out, and_5_out, and_6_out);
endmodule

module test (
  input  Reset,
  input  Start,
  output VDD,
  output GND
);

  wire affich_1_a, affich_1_b, affich_1_c, affich_1_d, affich_1_e, affich_1_f, affich_1_g, affich_2_a,
       affich_2_b, affich_2_c, affich_2_d, affich_2_e, affich_2_f, affich_2_g, affich_3_a, affich_3_b,
       affich_3_c, affich_3_d, affich_3_e, affich_3_f, affich_3_g, affich_4_a, affich_4_b, affich_4_c,
       affich_4_d, affich_4_e, affich_4_f, affich_4_g, clock_1_out, DipSwitch_1_sw1, DipSwitch_1_sw2,
       DipSwitch_1_sw3, DipSwitch_1_sw4, DipSwitch_1_sw5, DipSwitch_1_sw6, DipSwitch_1_sw7, DipSwitch_1_sw8,
       JEUSWITCH_1_led1, JEUSWITCH_1_led2, JEUSWITCH_1_led3, JEUSWITCH_1_led4, JEUSWITCH_1_led5,
       JEUSWITCH_1_led6, JEUSWITCH_1_led7, JEUSWITCH_1_led8, undriven, undriven_2, undriven_3;
  wire [3:0] JEUSWITCH_1_d_point, JEUSWITCH_1_d_sec_jeu, JEUSWITCH_1_u_point, JEUSWITCH_1_u_sec_jeu,
       undriven_4;

  DipSwitch DipSwitch_1 (
    .sw1(DipSwitch_1_sw1), .sw2(DipSwitch_1_sw2), .sw3(DipSwitch_1_sw3), .sw4(DipSwitch_1_sw4),
    .sw5(DipSwitch_1_sw5), .sw6(DipSwitch_1_sw6), .sw7(DipSwitch_1_sw7), .sw8(DipSwitch_1_sw8));
  DECOMPTEUR DECOMPTEUR_1 (
    .Clock(undriven), .Reset(undriven_2), .Trigger(1'b1), .D_sec_set(undriven_4), .SET_OK(undriven_3));  // open: D_h_set, U_h_set, D_min_set, U_min_set, U_sec_set, U_sec_Now, D_sec_Now, U_min_Now, D_min_Now, U_h_Now, D_h_Now
  Clock clock_1 (.out(clock_1_out));
  JEUREFLEXE JEUSWITCH_1 (
    .ME(1'b1), .DS1(DipSwitch_1_sw1), .DS2(DipSwitch_1_sw2), .DS3(DipSwitch_1_sw3), .DS4(DipSwitch_1_sw4),
    .DS5(DipSwitch_1_sw5), .DS6(DipSwitch_1_sw6), .DS7(DipSwitch_1_sw7), .DS8(DipSwitch_1_sw8),
    .ResetGame(Reset), .ResetTot(Start), .StartBTN(clock_1_out), .LED1(JEUSWITCH_1_led1),
    .LED2(JEUSWITCH_1_led2), .LED3(JEUSWITCH_1_led3), .LED4(JEUSWITCH_1_led4), .LED5(JEUSWITCH_1_led5),
    .LED6(JEUSWITCH_1_led6), .LED7(JEUSWITCH_1_led7), .LED8(JEUSWITCH_1_led8), .U_point(JEUSWITCH_1_u_point),
    .D_point(JEUSWITCH_1_d_point), .U_sec_jeu(JEUSWITCH_1_u_sec_jeu), .D_sec_jeu(JEUSWITCH_1_d_sec_jeu));  // open: Clock
  LED LED_1 (.in(JEUSWITCH_1_led1));
  LED LED_2 (.in(JEUSWITCH_1_led2));
  LED LED_3 (.in(JEUSWITCH_1_led3));
  LED LED_4 (.in(JEUSWITCH_1_led4));
  LED LED_5 (.in(JEUSWITCH_1_led5));
  LED LED_6 (.in(JEUSWITCH_1_led6));
  LED LED_7 (.in(JEUSWITCH_1_led7));
  LED LED_8 (.in(JEUSWITCH_1_led8));
  affich affich_1 (
    .a0(JEUSWITCH_1_u_point[3]), .b0(JEUSWITCH_1_u_point[2]), .c0(JEUSWITCH_1_u_point[1]),
    .d0(JEUSWITCH_1_u_point[0]), .a(affich_1_a), .b(affich_1_b), .c(affich_1_c), .d(affich_1_d),
    .e(affich_1_e), .f(affich_1_f), .g(affich_1_g));
  _7_Segment_Display L_7_Segment_Display_1 (
    .g(affich_1_g), .f(affich_1_f), .a(affich_1_a), .b(affich_1_b), .e(affich_1_e), .d(affich_1_d),
    .c(affich_1_c));  // open: dp
  affich affich_2 (
    .a0(JEUSWITCH_1_d_point[3]), .b0(JEUSWITCH_1_d_point[2]), .c0(JEUSWITCH_1_d_point[1]),
    .d0(JEUSWITCH_1_d_point[0]), .a(affich_2_a), .b(affich_2_b), .c(affich_2_c), .d(affich_2_d),
    .e(affich_2_e), .f(affich_2_f), .g(affich_2_g));
  _7_Segment_Display L_7_Segment_Display_2 (
    .g(affich_2_g), .f(affich_2_f), .a(affich_2_a), .b(affich_2_b), .e(affich_2_e), .d(affich_2_d),
    .c(affich_2_c));  // open: dp
  affich affich_3 (
    .a0(JEUSWITCH_1_u_sec_jeu[3]), .b0(JEUSWITCH_1_u_sec_jeu[2]), .c0(JEUSWITCH_1_u_sec_jeu[1]),
    .d0(JEUSWITCH_1_u_sec_jeu[0]), .a(affich_3_a), .b(affich_3_b), .c(affich_3_c), .d(affich_3_d),
    .e(affich_3_e), .f(affich_3_f), .g(affich_3_g));
  _7_Segment_Display L_7_Segment_Display_3 (
    .g(affich_3_g), .f(affich_3_f), .a(affich_3_a), .b(affich_3_b), .e(affich_3_e), .d(affich_3_d),
    .c(affich_3_c));  // open: dp
  affich affich_4 (
    .a0(JEUSWITCH_1_d_sec_jeu[3]), .b0(JEUSWITCH_1_d_sec_jeu[2]), .c0(JEUSWITCH_1_d_sec_jeu[1]),
    .d0(JEUSWITCH_1_d_sec_jeu[0]), .a(affich_4_a), .b(affich_4_b), .c(affich_4_c), .d(affich_4_d),
    .e(affich_4_e), .f(affich_4_f), .g(affich_4_g));
  _7_Segment_Display L_7_Segment_Display_4 (
    .g(affich_4_g), .f(affich_4_f), .a(affich_4_a), .b(affich_4_b), .e(affich_4_e), .d(affich_4_d),
    .c(affich_4_c));  // open: dp

  assign GND = 1'b0;
  assign VDD = 1'b1;
endmodule
